// Logisim project 658_Computer.circ as structural Verilog: 16 circuits, main circuit Motherboard
module Motherboard (
  input  in_1,
  input  in_2,
  input  in_3,
  input  in_4,
  input  in_5,
  input  in_6,
  input  in_7,
  input  in_8
);

  wire and_1_out, and_2_out, and_3_out, and_4_out, and_5_out, and_6_out, and_7_out, and_8_out, and_9_out,
       and_10_out, FST, gateway_latch_1_mread, gateway_latch_1_mvalid, gateway_latch_1_mwrite,
       microcontroller_board_1_1_main_memory_valid, microcontroller_board_1_1_rdy,
       microcontroller_board_1_1_read_enable_b, microcontroller_board_1_1_rwb,
       microcontroller_board_1_1_write_enable_b, nand_1_out, nand_2_out, or_1_out, or_2_out, or_3_out,
       or_4_out, or_5_out, pull_resistor_3_node, quick_timing_circuit_1_rst_1;
  wire [3:0] pull_resistor_2_node;
  wire [7:0] gateway_latch_1_xd_out, microcontroller_board_1_1_d_out, n3_to_8_decoder_lvc138_1_p5,
       pull_resistor_1_node, quick_timing_circuit_1_selector, ram_2_data;
  wire [23:0] gateway_latch_1_maddress_out_a0_23, microcontroller_board_1_1_address;
  wire [39:0] T1, T2;

  Quick_Timing_Circuit quick_timing_circuit_1 (
    .SELECTOR(quick_timing_circuit_1_selector), .CLK(FST), .RST_1(quick_timing_circuit_1_rst_1), .RESET(in_1));  // open: MULTIPLEXER, RST, RSTB, HCLK_B, COUNTER, HCLK, CLK_B
  Pull_Resistor pull_resistor_1 (.node(pull_resistor_1_node));
  Pull_Resistor #(.pull(1)) pull_resistor_2 (.node(pull_resistor_2_node));
  Microcontroller_Board_1 microcontroller_board_1_1 (
    .NMI_IN(pull_resistor_2_node), .D_IN(microcontroller_board_1_1_d_out),
    .D_OUT(microcontroller_board_1_1_d_out), .READ_ENABLE_B(microcontroller_board_1_1_read_enable_b),
    .RESET_1(quick_timing_circuit_1_rst_1), .IRQ_IN(pull_resistor_1_node),
    .MAIN_MEMORY_VALID(microcontroller_board_1_1_main_memory_valid),
    .SELECTOR(quick_timing_circuit_1_selector), .RWB(microcontroller_board_1_1_rwb),
    .WRITE_ENABLE_B(microcontroller_board_1_1_write_enable_b), .RDY(microcontroller_board_1_1_rdy),
    .ADDRESS(microcontroller_board_1_1_address));  // open: RESB_OUT, T1, IRQ_OUT, DEVICE_IDENTIFIER, T2, DEVICE_ADDRESS, FST, NMIB_OUT, DEVICE_CHANNEL, DEVICE_VALID_B
  // Device_Bus device_bus_1: pin names not known
  Gateway_Latch gateway_latch_1 (
    .TRANSFER_ENABLE(microcontroller_board_1_1_main_memory_valid), .MVALID(gateway_latch_1_mvalid),
    .OEBA(microcontroller_board_1_1_write_enable_b), .D_OUT(microcontroller_board_1_1_d_out),
    .ACCESS_SELECTOR_B(quick_timing_circuit_1_selector[0]), .RDY(microcontroller_board_1_1_rdy),
    .MREAD(gateway_latch_1_mread), .ADDRESS_IN_A0_23(microcontroller_board_1_1_address),
    .XD_OUT(gateway_latch_1_xd_out), .MWRITE(gateway_latch_1_mwrite), .D_IN(microcontroller_board_1_1_d_out),
    .XD_IN(gateway_latch_1_xd_out), .MADDRESS_OUT_A0_23(gateway_latch_1_maddress_out_a0_23),
    .OEAB(microcontroller_board_1_1_read_enable_b), .LEAB(microcontroller_board_1_1_rwb));  // open: MREADY
  Pull_Resistor pull_resistor_3 (.node(pull_resistor_3_node));
  // _3_to_8_Decoder__LVC138 3_to_8_decoder_lvc138_1: pin names not known; wires that end beside it: pull_resistor_3_node, pull_resistor_3_node, gateway_latch_1_maddress_out_a0_23[23:21], gateway_latch_1_mvalid, n3_to_8_decoder_lvc138_1_p5
  and and_1 (and_1_out, in_3, in_2);
  and and_2 (and_2_out, in_2, in_4);
  and and_3 (and_3_out, in_4, in_3);
  and and_4 (and_4_out, in_5, in_6);
  and and_5 (and_5_out, in_5, in_7);
  and and_6 (and_6_out, in_5, in_8);
  and and_7 (and_7_out, in_6, in_7);
  and and_8 (and_8_out, in_6, in_8);
  and and_9 (and_9_out, in_7, in_8);
  or or_1 (or_1_out, and_1_out, and_2_out, and_3_out);
  or or_2 (or_2_out, and_4_out, and_5_out);
  or or_3 (or_3_out, and_6_out, and_7_out);
  or or_4 (or_4_out, and_8_out, and_9_out);
  or or_5 (or_5_out, or_2_out, or_3_out, or_4_out);
  and and_10 (and_10_out, gateway_latch_1_mwrite, FST);
  nand nand_1 (nand_1_out, gateway_latch_1_mread, gateway_latch_1_mvalid);
  nand nand_2 (nand_2_out, and_10_out, gateway_latch_1_mvalid);
  // Probe on gateway_latch_1_maddress_out_a0_23[20:0]
  RAM #(.\type ("nonvolatile"), .addrWidth(21), .databus("bidir"), .enables("line"), .trigger("high")) ram_1 (
    .addr(gateway_latch_1_maddress_out_a0_23[20:0]), .data(gateway_latch_1_xd_out));  // open: we, oe, clk
  // NOT_Gate not_1 has open pins: in=nand_1_out, out=open
  // NOT_Gate not_2 has open pins: in=nand_2_out, out=open
  // NOT_Gate not_3 has open pins: in=n3_to_8_decoder_lvc138_1_p5[0], out=open
  RAM #(.addrWidth(21), .enables("line"), .databus("bidir"), .\type ("nonvolatile"), .trigger("high")) ram_2 (
    .addr(gateway_latch_1_maddress_out_a0_23[20:0]), .data(ram_2_data));  // open: we, oe, clk
  // NOT_Gate not_4 has open pins: in=nand_1_out, out=open
  // NOT_Gate not_5 has open pins: in=nand_2_out, out=open
  // NOT_Gate not_6 has open pins: in=n3_to_8_decoder_lvc138_1_p5[1], out=open
  RAM #(.\type ("nonvolatile"), .trigger("high"), .addrWidth(21), .enables("line"), .databus("bidir")) ram_3 (
    .addr(gateway_latch_1_maddress_out_a0_23[20:0]), .data(ram_2_data));  // open: we, oe, clk
  // NOT_Gate not_7 has open pins: in=nand_1_out, out=open
  // NOT_Gate not_8 has open pins: in=nand_2_out, out=open
  // NOT_Gate not_9 has open pins: in=n3_to_8_decoder_lvc138_1_p5[2], out=open
  RAM #(.trigger("high"), .enables("line"), .\type ("nonvolatile"), .addrWidth(21), .databus("bidir")) ram_4 (
    .addr(gateway_latch_1_maddress_out_a0_23[20:0]), .data(ram_2_data));  // open: we, oe, clk
  // NOT_Gate not_10 has open pins: in=nand_1_out, out=open
  // NOT_Gate not_11 has open pins: in=nand_2_out, out=open
  // NOT_Gate not_12 has open pins: in=n3_to_8_decoder_lvc138_1_p5[3], out=open
  // Probe on gateway_latch_1_xd_out
  // Helper__W65C816_Timing helper_w65c816_timing_1: pin names not known; wires that end beside it: 4'b0110, 4'b0001, 4'b0110, 4'b0100, 4'b0001, 4'b0101, 4'b0001, 4'b0110, 4'b0010, 4'b0110, FST, T1, 4'b0100, 4'b0000, 4'b0111, 4'b0000, 4'b0011, 4'b0111, 4'b0111, 4'b0000, 4'b0011, 4'b0000, T2

  // Notes on the sheet:
  //   ANDing this with clock is required to turn the write off before the address and data are turned off.
endmodule

module Microcontroller_Board_0 (
  input  in_1,
  input  [7:0] IRQ,
  input  [3:0] NMI
);

  wire and_2_out, BANK_LATCH, CLOCK_ENABLE_B, CS0_B, CS1_B, CS2_B, CS3_B, DATA_TRANSMIT_B,
       DEVICE_ADDRESS_VALID_B, ENTER_INTERRUPT, EXIT_INTERRUPT, FST, INTERNAL_MEMORY_ADDRESS_VALID,
       internal_memory_glue_1_ceb, internal_memory_glue_1_oeb, internal_memory_glue_1_web, IRQ_B,
       KERNAL_MODE, KERNAL_MODE_B, KERNAL_ROM_B, MAIN_MEMORY_ADDRESS_VALID, microprocessor_w65c816_1_p6,
       microprocessor_w65c816_1_p13, microprocessor_w65c816_1_p14, microprocessor_w65c816_1_p15,
       MRAM_ACCESS_B, MREAD, MREADY, MVALID, MWRITE, n8_bit_bi_latch_lvc543_1_p5,
       n8_bit_bi_latch_lvc543_2_p5, n8_bit_bi_latch_lvc543_3_p8, n8_bit_comparator_f521_1_p4,
       n16_bit_latch_lvc16373_1_p7, n16_bit_latch_lvc16373_1_p8, nand_1_out, nand_2_out, NATIVE_MODE, NMI_B,
       nor_1_out, not_1_out, not_2_out, not_3_out, not_4_out, not_5_out, not_6_out, not_7_out, not_8_out,
       not_9_out, not_10_out, not_11_out, not_12_out, not_13_out, not_14_out, not_15_out, not_16_out,
       not_20_out, not_21_out, not_22_out, OPCODE_ADDRESS, or_1_out, or_2_out, or_3_out, or_4_out, or_5_out,
       or_6_out, PHI2, pull_resistor_3_node, pull_resistor_4_node, pull_resistor_8_node,
       pull_resistor_11_node, pull_resistor_12_node, pull_resistor_19_node, PULSE_0, PULSE_1, PULSE_2,
       quick_timing_circuit_1_clk, quick_timing_circuit_1_rst_1, RDY, READ_BANK_REMAP_B, READ_ENABLE,
       READ_ENABLE_B, READ_SELECTOR, RESET, ROM_ADDRESS_VALID, RWB, RWB_B, SA_FLAG_REGISTER_B,
       SA_INTERRUPTS_IN_DEPTH_B, SA_SHORT_PULSE_OUT_B, SA_USER_PROGRAM_ID_B, SEL0, SEL2, SEL4, SEL6,
       selector_state_1_sel0, selector_state_1_sel1, selector_state_1_sel2, selector_state_1_sel3,
       selector_state_1_sel4, selector_state_1_sel5, selector_state_1_sel6, selector_state_1_sel7,
       SPECIAL_ADDRESS_VALID_B, STOP_SELECTOR, VPB, WRITE_ENABLE, WRITE_ENABLE_B, WRITE_SELECTOR;
  wire [0:0] flags_and_pulse_1_flag_register;
  wire [1:0] DEVICE_CHANNEL, n16_bit_line_driver_lvc16244_1_p8, pull_resistor_6_node;
  wire [2:0] IRQ_MPU0_2, RES_MPU0_2B;
  wire [3:0] DEVICE_ADDRESS, n2_to_4_decoder_lvc139_1_p4, n16_bit_line_driver_lvc16244_1_p10,
       pull_resistor_7_node;
  wire [5:0] DEVICE_IDENTIFIER, n16_bit_line_driver_lvc16244_1_p9;
  wire [7:0] A0_7, A8_15, BA0_7, D, interrupt_detection_1_opcode, IRAM_A0_7, KERNAL_ROM_data,
       kernal_user_mode_1_interrupt_depth, microprocessor_w65c816_1_p10, MRAM_A16_23,
       n8_bit_bi_latch_lvc543_3_p5, ram_2_data, USER_PROGRAM_ID;
  wire [7:1] quick_timing_circuit_1_selector;
  wire [7:4] n3_to_8_decoder_lvc138_1_p5;
  wire [15:4] address_decode_1_special_memory_selector_b;
  wire [16:0] internal_memory_glue_1_address_out_a0_16;
  wire [23:0] MRAM_A;
  wire [39:0] T1, T2;

  Quick_Timing_Circuit quick_timing_circuit_1 (
    .SELECTOR({quick_timing_circuit_1_selector[7], SEL6, quick_timing_circuit_1_selector[5], SEL4, quick_timing_circuit_1_selector[3], SEL2, quick_timing_circuit_1_selector[1], SEL0}),
    .CLK(quick_timing_circuit_1_clk), .RST_1(quick_timing_circuit_1_rst_1), .RESET(in_1));  // open: MULTIPLEXER, RST, RSTB, HCLK_B, COUNTER, HCLK, CLK_B
  not not_1 (not_1_out, PHI2);
  // Probe on {BA0_7, A8_15, A0_7}
  // Probe on D
  not not_2 (not_2_out, IRQ[0]);
  not not_3 (not_3_out, IRQ[1]);
  not not_4 (not_4_out, IRQ[2]);
  not not_5 (not_5_out, IRQ[3]);
  not not_6 (not_6_out, IRQ[4]);
  not not_7 (not_7_out, IRQ[5]);
  not not_8 (not_8_out, IRQ[6]);
  not not_9 (not_9_out, IRQ[7]);
  not not_10 (not_10_out, NMI[0]);
  not not_11 (not_11_out, NMI[1]);
  not not_12 (not_12_out, NMI[2]);
  not not_13 (not_13_out, NMI[3]);
  LED led_1 (.in(selector_state_1_sel0));
  LED led_2 (.in(selector_state_1_sel1));
  Interrupt_Detection interrupt_detection_1 (
    .ENTER_INTERRUPT(ENTER_INTERRUPT), .OPCODE_ADDRESS(OPCODE_ADDRESS),
    .OPCODE(interrupt_detection_1_opcode), .D(D), .LATCH_D(WRITE_SELECTOR),
    .RETURN_FROM_INTERRUPT(EXIT_INTERRUPT), .RESET_B(RESET), .NATIVE_MODE(NATIVE_MODE),
    .ADDRESS_IN_A0(A0_7[0]), .PHI2_B(not_1_out));
  LED led_3 (.in(selector_state_1_sel2));
  LED led_4 (.in(selector_state_1_sel5));
  LED led_5 (.in(selector_state_1_sel3));
  LED led_6 (.in(selector_state_1_sel4));
  Selector_State selector_state_1 (
    .STOP_SELECTOR(STOP_SELECTOR), .SEL6(selector_state_1_sel6), .DATA_TRANSMIT_B(DATA_TRANSMIT_B),
    .SELECTOR({quick_timing_circuit_1_selector[7], SEL6, quick_timing_circuit_1_selector[5], SEL4, quick_timing_circuit_1_selector[3], SEL2, quick_timing_circuit_1_selector[1], SEL0}),
    .SEL1(selector_state_1_sel1), .SEL0(selector_state_1_sel0), .RESET(quick_timing_circuit_1_rst_1),
    .READ_SELECTOR(READ_SELECTOR), .PHI2(PHI2), .READ_BANK_REMAP_B(READ_BANK_REMAP_B),
    .WRITE_SELECTOR(WRITE_SELECTOR), .SEL3(selector_state_1_sel3), .CLOCK_ENABLE_B(CLOCK_ENABLE_B),
    .SEL2(selector_state_1_sel2), .BANK_LATCH(BANK_LATCH), .MRAM_ACCESS_B(MRAM_ACCESS_B),
    .SEL4(selector_state_1_sel4), .SEL7(selector_state_1_sel7), .BOARD_RESET(RESET),
    .SEL5(selector_state_1_sel5));
  not not_14 (not_14_out, CLOCK_ENABLE_B);
  Address_Decode address_decode_1 (
    .DEVICE_CHANNEL(DEVICE_CHANNEL), .KERNAL_MODE(KERNAL_MODE), .ROM_VALID(ROM_ADDRESS_VALID),
    .SPECIAL_VALID_B(SPECIAL_ADDRESS_VALID_B),
    .SPECIAL_MEMORY_SELECTOR_B({address_decode_1_special_memory_selector_b, SA_SHORT_PULSE_OUT_B, SA_FLAG_REGISTER_B, SA_INTERRUPTS_IN_DEPTH_B, SA_USER_PROGRAM_ID_B}),
    .DEVICE_ADDRESS(DEVICE_ADDRESS), .KERNAL_ROM_B(KERNAL_ROM_B), .ADDRESS_IN_A0_24({BA0_7, A8_15, A0_7}),
    .DEVICE_VALID_B(DEVICE_ADDRESS_VALID_B), .MAIN_MEMORY_VALID(MAIN_MEMORY_ADDRESS_VALID), .RWB(RWB),
    .DEVICE_IDENTIFIER(DEVICE_IDENTIFIER), .KERNAL_MODE_B(KERNAL_MODE_B),
    .INTERNAL_RAM_VALID(INTERNAL_MEMORY_ADDRESS_VALID));
  Clock_Control clock_control_1 (
    .UNSTOPPABLE_CLOCK(STOP_SELECTOR), .CLOCK_ENABLE_B(CLOCK_ENABLE_B), .RESET(RESET),
    .ROM_ADDRESS_VALID(ROM_ADDRESS_VALID), .DEVICE_ADDRESS_VALID_B(DEVICE_ADDRESS_VALID_B), .RWB_B(RWB_B));
  Interrupt_Vectoring interrupt_vectoring_1 (
    .IRQ_3_B(not_5_out), .IRQ_1_B(not_3_out), .IRQ_4_B(not_6_out), .IRQ_5_B(not_7_out), .VPB(VPB),
    .IRQ_7_B(not_9_out), .NMI_B(NMI_B), .NMI_0_B(not_10_out), .NMI_1_B(not_11_out), .NMI_3_B(not_13_out),
    .IRQ_B(IRQ_B), .NMI_2_B(not_12_out), .ADDRESS_IN_A0_7(A0_7), .IRQ_0_B(not_2_out), .IRQ_6_B(not_8_out),
    .IRQ_2_B(not_4_out), .ADDRESS_OUT_A0_7(IRAM_A0_7));
  LED led_7 (.in(selector_state_1_sel7));
  LED led_8 (.in(selector_state_1_sel6));
  and and_1 (FST, not_14_out, quick_timing_circuit_1_clk);
  Counter #(.max('hffffffff), .width(32)) counter_1 (.clk(FST));  // open: load, D, count, Q, carry, up, clr
  // Probe on interrupt_detection_1_opcode
  or or_1 (or_1_out, RWB_B, SEL4);
  // Probe on D
  or or_2 (or_2_out, DEVICE_ADDRESS_VALID_B, SEL4);
  Pull_Resistor #(.pull(1)) pull_resistor_1 ();  // open: node
  Pull_Resistor #(.pull(1)) pull_resistor_2 ();  // open: node
  Pull_Resistor #(.pull(1)) pull_resistor_3 (.node(pull_resistor_3_node));
  LED led_9 (.in(INTERNAL_MEMORY_ADDRESS_VALID));
  LED led_10 (.in(SPECIAL_ADDRESS_VALID_B));
  LED led_11 (.in(DEVICE_ADDRESS_VALID_B));
  LED led_12 (.in(ROM_ADDRESS_VALID));
  LED led_13 (.in(MAIN_MEMORY_ADDRESS_VALID));
  // _8_bit_Bi_latch__LVC543 8_bit_bi_latch_lvc543_1: pin names not known; wires that end beside it: RWB, RWB, SEL4, D, n8_bit_bi_latch_lvc543_1_p5, or_1_out, RWB_B, DEVICE_ADDRESS_VALID_B
  // _16_bit_Line_Driver__LVC16244 16_bit_line_driver_lvc16244_1: pin names not known; wires that end beside it: SEL4, SEL4, SEL4, SEL4, {DEVICE_IDENTIFIER[5:4], WRITE_ENABLE_B, READ_ENABLE_B}, DEVICE_IDENTIFIER[3:0], DEVICE_ADDRESS, {n16_bit_line_driver_lvc16244_1_p9[5:4], n16_bit_line_driver_lvc16244_1_p8}, n16_bit_line_driver_lvc16244_1_p9[3:0], n16_bit_line_driver_lvc16244_1_p10
  // _2_to_4_Decoder__LVC139 2_to_4_decoder_lvc139_1: pin names not known; wires that end beside it: or_2_out, DEVICE_CHANNEL, pull_resistor_3_node, n2_to_4_decoder_lvc139_1_p4
  Pull_Resistor #(.pull(1)) pull_resistor_4 (.node(pull_resistor_4_node));
  // Microprocessor__W65C816 microprocessor_w65c816_1: pin names not known; wires that end beside it: pull_resistor_4_node, IRQ_B, NMI_B, RESET, PHI2, microprocessor_w65c816_1_p6, T1, T2, {A8_15, A0_7}, microprocessor_w65c816_1_p10, RWB, RDY, microprocessor_w65c816_1_p13, microprocessor_w65c816_1_p14, microprocessor_w65c816_1_p15, FST, VPB
  Kernal_User_Mode kernal_user_mode_1 (
    .KERNAL_MODE_B2(KERNAL_MODE_B), .ENTER_INTERRUPT(ENTER_INTERRUPT), .USER(USER_PROGRAM_ID),
    .EXIT_INTERRUPT(EXIT_INTERRUPT), .D_OUT(D), .INTERRUPT_DEPTH(kernal_user_mode_1_interrupt_depth),
    .RESET(RESET), .D_IN(D), .READ_ENABLE_B(READ_ENABLE_B), .KERNAL_MODE2(KERNAL_MODE),
    .WRITE_ENABLE_B(WRITE_ENABLE_B), .SA_USER_PROGRAM_ID_B(SA_USER_PROGRAM_ID_B),
    .SA_INTERRUPTS_IN_DEPTH_B(SA_INTERRUPTS_IN_DEPTH_B));
  Flags_And_Pulse flags_and_pulse_1 (
    .SA_FLAG_REGISTER_B(SA_FLAG_REGISTER_B), .D_OUT(D), .RESET(RESET), .PULSE_2(PULSE_2),
    .WRITE_ENABLE_B(WRITE_ENABLE_B), .PULSE_0(PULSE_0), .READ_ENABLE_B(READ_ENABLE_B),
    .FLAG_REGISTER({RES_MPU0_2B, IRQ_MPU0_2, KERNAL_ROM_B, flags_and_pulse_1_flag_register[0]}),
    .SA_SHORT_PULSE_OUT_B(SA_SHORT_PULSE_OUT_B), .PHI2(PHI2), .PULSE_1(PULSE_1), .D_IN(D));
  // Probe on {A8_15, A0_7}
  Pull_Resistor #(.pull(1)) pull_resistor_5 (.node(microprocessor_w65c816_1_p15));
  Pull_Resistor pull_resistor_6 (.node(pull_resistor_6_node));
  Pull_Resistor pull_resistor_7 (.node(pull_resistor_7_node));
  // Probe on microprocessor_w65c816_1_p10
  // Probe on {BA0_7, A8_15, IRAM_A0_7}
  // Probe on USER_PROGRAM_ID
  // Probe on kernal_user_mode_1_interrupt_depth
  Pull_Resistor pull_resistor_8 (.node(pull_resistor_8_node));
  not not_15 (not_15_out, n2_to_4_decoder_lvc139_1_p4[0]);
  Internal_Memory_Glue internal_memory_glue_1 (
    .READ_BANK_REMAP_B(READ_BANK_REMAP_B), .ADDRESS_IN_A0_23({BA0_7, A8_15, IRAM_A0_7}),
    .READ_ENABLE(READ_ENABLE), .INTERNAL_MEMORY_VALID(INTERNAL_MEMORY_ADDRESS_VALID),
    .WRITE_ENABLE(WRITE_ENABLE), .CEB(internal_memory_glue_1_ceb),
    .ADDRESS_OUT_A0_16(internal_memory_glue_1_address_out_a0_16), .WEB(internal_memory_glue_1_web),
    .OEB(internal_memory_glue_1_oeb), .USER_BANK(USER_PROGRAM_ID));
  // _8_bit_Bi_latch__LVC543 8_bit_bi_latch_lvc543_2: pin names not known; wires that end beside it: n16_bit_line_driver_lvc16244_1_p8[1], n16_bit_line_driver_lvc16244_1_p8[1], n2_to_4_decoder_lvc139_1_p4[0], n8_bit_bi_latch_lvc543_1_p5, n8_bit_bi_latch_lvc543_2_p5, n16_bit_line_driver_lvc16244_1_p8[0], n16_bit_line_driver_lvc16244_1_p8[0], n2_to_4_decoder_lvc139_1_p4[0]
  // _16_bit_Latch__LVC16373 16_bit_latch_lvc16373_1: pin names not known; wires that end beside it: pull_resistor_8_node, pull_resistor_8_node, {pull_resistor_6_node, n16_bit_line_driver_lvc16244_1_p9}, not_15_out, {pull_resistor_7_node, n16_bit_line_driver_lvc16244_1_p10}, not_15_out, n16_bit_latch_lvc16373_1_p7, n16_bit_latch_lvc16373_1_p8
  Pull_Resistor pull_resistor_9 (.node({A8_15, A0_7}));
  // _8_bit_Bus_Transceiver__LVC4245 8_bit_bus_transceiver_lvc4245_1: pin names not known; wires that end beside it: DATA_TRANSMIT_B, microprocessor_w65c816_1_p10, RWB, D
  Signals signals_1 (
    .VDA(microprocessor_w65c816_1_p13), .RWB(RWB), .WRITE_SELECTOR(WRITE_SELECTOR),
    .CLOCK_ENABLE_B(CLOCK_ENABLE_B), .E(microprocessor_w65c816_1_p6), .NATIVE_MODE(NATIVE_MODE),
    .BANK_LATCH(BANK_LATCH), .READ_ENABLE_B(READ_ENABLE_B), .BA0_7(BA0_7), .WRITE_ENABLE(WRITE_ENABLE),
    .READ_SELECTOR(READ_SELECTOR), .READ_ENABLE(READ_ENABLE), .RWB_B(RWB_B),
    .D(microprocessor_w65c816_1_p10), .OPCODE_ADDRESS(OPCODE_ADDRESS), .WRITE_ENABLE_B(WRITE_ENABLE_B),
    .VPA(microprocessor_w65c816_1_p14));
  not not_16 (not_16_out, ROM_ADDRESS_VALID);
  // Probe on internal_memory_glue_1_address_out_a0_16
  RAM #(.trigger("high"), .enables("line"), .databus("bidir"), .addrWidth(17), .\type ("nonvolatile")) INTERNAL_MEMORY (
    .addr(internal_memory_glue_1_address_out_a0_16), .data(D));  // open: we, oe, clk
  LED led_14 (.in(internal_memory_glue_1_oeb));
  // NOT_Gate not_17 has open pins: in=internal_memory_glue_1_oeb, out=open
  // NOT_Gate not_18 has open pins: in=internal_memory_glue_1_web, out=open
  LED led_15 (.in(internal_memory_glue_1_web));
  // NOT_Gate not_19 has open pins: in=internal_memory_glue_1_ceb, out=open
  // Probe on {A8_15[6:0], IRAM_A0_7}
  LED led_16 (.in(or_3_out));
  or or_3 (or_3_out, not_16_out, READ_ENABLE_B);
  not not_20 (not_20_out, READ_BANK_REMAP_B);
  // Probe on {BA0_7, A8_15, A0_7}
  Pull_Resistor pull_resistor_10 (.node(D));
  ROM #(.addrWidth(16)) KERNAL_ROM (.addr({1'b1, A8_15[6:0], IRAM_A0_7}), .data(KERNAL_ROM_data));
  not not_21 (not_21_out, or_3_out);
  // _8_bit_Latch__LVC573 8_bit_latch_lvc573_1: pin names not known; wires that end beside it: KERNAL_MODE, D, not_20_out, MRAM_A16_23
  // _8_bit_Line_Driver__LVC541 8_bit_line_driver_lvc541_1: pin names not known; wires that end beside it: KERNAL_MODE_B, KERNAL_MODE_B, BA0_7, MRAM_A16_23
  // Probe on n8_bit_bi_latch_lvc543_2_p5
  // Probe on MRAM_A16_23
  // Probe on D
  assign D = not_21_out ? KERNAL_ROM_data : 8'bz;  // Controlled_Buffer controlled_buffer_1
  // Probe on n16_bit_latch_lvc16373_1_p7
  // Probe on n16_bit_latch_lvc16373_1_p8
  // Probe on D
  not not_22 (not_22_out, MAIN_MEMORY_ADDRESS_VALID);
  or or_4 (or_4_out, READ_ENABLE_B, n8_bit_comparator_f521_1_p4);
  nor nor_1 (nor_1_out, WRITE_ENABLE_B, n8_bit_comparator_f521_1_p4);
  // _8_bit_Comparator__F521 8_bit_comparator_f521_1: pin names not known; wires that end beside it: DEVICE_ADDRESS_VALID_B, n16_bit_latch_lvc16373_1_p7, {8{1'b0}}, n8_bit_comparator_f521_1_p4
  or or_5 (or_5_out, READ_ENABLE_B, MRAM_ACCESS_B, not_22_out);
  or or_6 (or_6_out, WRITE_ENABLE_B, MRAM_ACCESS_B, not_22_out);
  // Probe on D
  // _8_bit_Latch__LVC573 8_bit_latch_lvc573_2: pin names not known; wires that end beside it: or_4_out, n8_bit_bi_latch_lvc543_2_p5, nor_1_out, n8_bit_bi_latch_lvc543_2_p5
  Pull_Resistor pull_resistor_11 (.node(pull_resistor_11_node));
  Pull_Resistor #(.pull(1)) pull_resistor_12 (.node(pull_resistor_12_node));
  // _8_bit_Bi_latch__LVC543 8_bit_bi_latch_lvc543_3: pin names not known; wires that end beside it: RWB, or_6_out, pull_resistor_11_node, D, n8_bit_bi_latch_lvc543_3_p5, RWB_B, or_5_out, n8_bit_bi_latch_lvc543_3_p8
  // _16_bit_Line_Driver__LVC16244 16_bit_line_driver_lvc16244_2: pin names not known; wires that end beside it: pull_resistor_12_node, MRAM_ACCESS_B, MRAM_ACCESS_B, MRAM_ACCESS_B, {RDY, MAIN_MEMORY_ADDRESS_VALID, RWB_B, RWB}, MRAM_A16_23[3:0], MRAM_A16_23[7:4], {MREADY, MVALID, MWRITE, MREAD}, MRAM_A[19:16], MRAM_A[23:20]
  // _16_bit_Line_Driver__LVC16244 16_bit_line_driver_lvc16244_3: pin names not known; wires that end beside it: MRAM_ACCESS_B, MRAM_ACCESS_B, MRAM_ACCESS_B, MRAM_ACCESS_B, A8_15[7:4], A8_15[3:0], A0_7[7:4], A0_7[3:0], MRAM_A[15:12], MRAM_A[11:8], MRAM_A[7:4], MRAM_A[3:0]
  Pull_Resistor pull_resistor_13 (.node(n8_bit_bi_latch_lvc543_3_p8));
  Pull_Resistor pull_resistor_14 (.node(MREAD));
  Pull_Resistor pull_resistor_15 (.node(MWRITE));
  Pull_Resistor pull_resistor_16 (.node(MVALID));
  Pull_Resistor pull_resistor_17 (.node(MREADY));
  // Probe on MRAM_A
  Pull_Resistor pull_resistor_18 (.node(MRAM_A));
  Pull_Resistor pull_resistor_19 (.node(pull_resistor_19_node));
  and and_2 (and_2_out, MWRITE, FST);
  // _3_to_8_Decoder__LVC138 3_to_8_decoder_lvc138_1: pin names not known; wires that end beside it: pull_resistor_19_node, pull_resistor_19_node, MRAM_A[23:21], MVALID, {n3_to_8_decoder_lvc138_1_p5, CS3_B, CS2_B, CS1_B, CS0_B}
  nand nand_1 (nand_1_out, MREAD, MVALID);
  nand nand_2 (nand_2_out, and_2_out, MVALID);
  // Probe on MRAM_A[20:0]
  RAM #(.addrWidth(21), .databus("bidir"), .\type ("nonvolatile"), .trigger("high"), .enables("line")) ram_1 (
    .addr(MRAM_A[20:0]), .data(n8_bit_bi_latch_lvc543_3_p5));  // open: we, oe, clk
  // NOT_Gate not_23 has open pins: in=nand_1_out, out=open
  // NOT_Gate not_24 has open pins: in=nand_2_out, out=open
  // NOT_Gate not_25 has open pins: in=CS0_B, out=open
  RAM #(.trigger("high"), .databus("bidir"), .addrWidth(21), .\type ("nonvolatile"), .enables("line")) ram_2 (
    .addr(MRAM_A[20:0]), .data(ram_2_data));  // open: we, oe, clk
  // NOT_Gate not_26 has open pins: in=nand_1_out, out=open
  // NOT_Gate not_27 has open pins: in=nand_2_out, out=open
  // NOT_Gate not_28 has open pins: in=CS1_B, out=open
  RAM #(.databus("bidir"), .trigger("high"), .enables("line"), .\type ("nonvolatile"), .addrWidth(21)) ram_3 (
    .addr(MRAM_A[20:0]), .data(ram_2_data));  // open: we, oe, clk
  // NOT_Gate not_29 has open pins: in=nand_1_out, out=open
  // NOT_Gate not_30 has open pins: in=nand_2_out, out=open
  // NOT_Gate not_31 has open pins: in=CS2_B, out=open
  RAM #(.databus("bidir"), .trigger("high"), .addrWidth(21), .enables("line"), .\type ("nonvolatile")) ram_4 (
    .addr(MRAM_A[20:0]), .data(ram_2_data));  // open: we, oe, clk
  // NOT_Gate not_32 has open pins: in=nand_1_out, out=open
  // NOT_Gate not_33 has open pins: in=nand_2_out, out=open
  // NOT_Gate not_34 has open pins: in=CS3_B, out=open
  // Probe on n8_bit_bi_latch_lvc543_3_p5
  // Helper__W65C816_Timing helper_w65c816_timing_1: pin names not known; wires that end beside it: PHI2, 4'b0110, 4'b0001, 4'b0110, 4'b0100, 4'b0001, 4'b0101, 4'b0001, 4'b0110, 4'b0010, 4'b0110, FST, T1, 4'b0100, 4'b0000, 4'b0111, 4'b0000, 4'b0011, 4'b0111, 4'b0111, 4'b0000, 4'b0011, 4'b0000, T2

  // Other names for the same wires on the sheet: MRAM_A0_20[20:0] = MRAM_A[20:0]

  // Notes on the sheet:
  //   Device Channel 0
  //   contents of KERNAL_ROM (hex, n*v repeats v):
  //   16384*0 ad fc ff c9 2b e1 f0 2 0 0 e2 20 a9 a4 8d 0 70 a9 cc ad 0 70 1a 8d 0 70 a9 cc ad 0 70 c9 a5
  //   f0 2 0 0 a9 ff 8d 0 6f a9 2 8f 0 ff 1 a9 3 8f 1 ff 1 a9 0 48 a9 4 48 a9 1c 48 8 40 41194*ff 18 fb c2
  //   30 a9 ff 1 1b e2 20 a9 0 48 ab c2 20 5c 0 40 0 8b b c2 30 48 da 5a 80 2d 8b b c2 30 48 da 5a 80 24
  //   8b b c2 30 48 da 5a 80 1b 8b b c2 30 48 da 5a 80 12 8b b c2 30 48 da 5a 80 9 8b b c2 30 48 da 5a 80
  //   0 c2 30 7a fa 68 2b ab 40 7783*ff 5a e1 63 e1 51 e1 48 e1 0 0 3f e1 4*ff 6c e1 0 0 6c e1 6c e1 2b e1
  //   6c e1
  //   32KB_ROM
  //   ANDing this with clock is required to turn the write off before the address and data are turned off.
endmodule

module Microcontroller_Board_1 (
  input  RESET_1,
  input  [7:0] SELECTOR,
  input  FST,
  input  [39:0] T1,
  input  [39:0] T2,
  input  [7:0] D_IN,
  input  [7:0] IRQ_IN,
  input  [3:0] NMI_IN,
  output [23:0] ADDRESS,
  output READ_ENABLE_B,
  output WRITE_ENABLE_B,
  output MAIN_MEMORY_VALID,
  output RWB,
  output RDY,
  output [2:0] IRQ_OUT,
  output [2:0] RESB_OUT,
  output [2:0] NMIB_OUT,
  output [7:0] D_OUT,
  output DEVICE_VALID_B,
  output [1:0] DEVICE_CHANNEL,
  output [5:0] DEVICE_IDENTIFIER,
  output [3:0] DEVICE_ADDRESS
);

  wire and_2_out, and_3_out, BANK_LATCH, CLOCK_ENABLE_B, DATA_TRANSMIT_B, FST_t, INTERNAL_MEMORY_VALID,
       IRQ_B, KERNAL_ROM_B, microprocessor_w65c816_1_p6, microprocessor_w65c816_1_p13,
       microprocessor_w65c816_1_p14, microprocessor_w65c816_1_p15, MRAM_ACCESS_B, nand_1_out, nand_2_out,
       NATIVE_MODE, NMI_B, not_1_out, not_2_out, not_3_out, not_4_out, not_5_out, not_6_out, not_7_out,
       not_8_out, not_9_out, not_10_out, not_14_out, OPCODE_ADDRESS, or_1_out, PHI2, pull_resistor_1_node,
       pull_resistor_2_node, pull_resistor_3_node, pull_resistor_7_node, READ_ENABLE, READ_SELECTOR, RESET,
       ROM_ADDRESS_VALID, RWB_B, SA_FLAG_REGISTER_B, SA_SHORT_PULSE_OUT_B, selector_state_1_sel0,
       selector_state_1_sel1, selector_state_1_sel2, selector_state_1_sel3, selector_state_1_sel4,
       selector_state_1_sel5, selector_state_1_sel6, selector_state_1_sel7, SPECIAL_ADDRESS_VALID_B,
       STOP_SELECTOR, VPB, WRITE_ENABLE, WRITE_SELECTOR;
  wire [0:0] flags_and_pulse_1_flag_register;
  wire [7:0] D, IRAM_A0_7, KERNAL_ROM_data, microprocessor_w65c816_1_p10;
  wire [15:0] address_decode_1_special_memory_selector_b;

  LED led_1 (.in(selector_state_1_sel2));
  LED led_2 (.in(selector_state_1_sel0));
  LED led_3 (.in(selector_state_1_sel1));
  LED led_4 (.in(selector_state_1_sel6));
  LED led_5 (.in(selector_state_1_sel5));
  LED led_6 (.in(selector_state_1_sel4));
  LED led_7 (.in(selector_state_1_sel3));
  Selector_State selector_state_1 (
    .STOP_SELECTOR(STOP_SELECTOR), .SEL6(selector_state_1_sel6), .DATA_TRANSMIT_B(DATA_TRANSMIT_B),
    .SELECTOR(SELECTOR), .SEL1(selector_state_1_sel1), .SEL0(selector_state_1_sel0), .RESET(RESET_1),
    .READ_SELECTOR(READ_SELECTOR), .PHI2(PHI2), .WRITE_SELECTOR(WRITE_SELECTOR),
    .SEL3(selector_state_1_sel3), .CLOCK_ENABLE_B(CLOCK_ENABLE_B), .SEL2(selector_state_1_sel2),
    .BANK_LATCH(BANK_LATCH), .MRAM_ACCESS_B(MRAM_ACCESS_B), .SEL4(selector_state_1_sel4),
    .SEL7(selector_state_1_sel7), .BOARD_RESET(RESET), .SEL5(selector_state_1_sel5));  // open: READ_BANK_REMAP_B
  not not_1 (not_1_out, CLOCK_ENABLE_B);
  and and_1 (FST_t, not_1_out, FST);
  Flags_And_Pulse flags_and_pulse_1 (
    .SA_FLAG_REGISTER_B(SA_FLAG_REGISTER_B), .D_OUT(D), .RESET(RESET), .PULSE_2(NMIB_OUT[2]),
    .WRITE_ENABLE_B(WRITE_ENABLE_B), .PULSE_0(NMIB_OUT[0]), .READ_ENABLE_B(READ_ENABLE_B),
    .FLAG_REGISTER({RESB_OUT, IRQ_OUT, KERNAL_ROM_B, flags_and_pulse_1_flag_register[0]}),
    .SA_SHORT_PULSE_OUT_B(SA_SHORT_PULSE_OUT_B), .PHI2(PHI2), .PULSE_1(NMIB_OUT[1]), .D_IN(D));
  LED led_8 (.in(selector_state_1_sel7));
  Counter #(.max('hffffffff), .width(32)) counter_1 (.clk(FST_t));  // open: load, D, count, Q, carry, up, clr
  Pull_Resistor #(.pull(1)) pull_resistor_1 (.node(pull_resistor_1_node));
  Pull_Resistor pull_resistor_2 (.node(pull_resistor_2_node));
  Pull_Resistor #(.pull(1)) pull_resistor_3 (.node(pull_resistor_3_node));
  not not_2 (not_2_out, IRQ_IN[0]);
  not not_3 (not_3_out, IRQ_IN[1]);
  not not_4 (not_4_out, IRQ_IN[2]);
  not not_5 (not_5_out, IRQ_IN[3]);
  not not_6 (not_6_out, IRQ_IN[4]);
  not not_7 (not_7_out, IRQ_IN[5]);
  not not_8 (not_8_out, IRQ_IN[6]);
  not not_9 (not_9_out, IRQ_IN[7]);
  // Probe on ADDRESS
  // Microprocessor__W65C816 microprocessor_w65c816_1: pin names not known; wires that end beside it: pull_resistor_3_node, IRQ_B, NMI_B, RESET, PHI2, microprocessor_w65c816_1_p6, T1, T2, ADDRESS[15:0], microprocessor_w65c816_1_p10, RWB, RDY, microprocessor_w65c816_1_p13, microprocessor_w65c816_1_p14, microprocessor_w65c816_1_p15, FST_t, VPB
  Address_Decode address_decode_1 (
    .DEVICE_CHANNEL(DEVICE_CHANNEL), .KERNAL_MODE(pull_resistor_1_node), .ROM_VALID(ROM_ADDRESS_VALID),
    .SPECIAL_VALID_B(SPECIAL_ADDRESS_VALID_B),
    .SPECIAL_MEMORY_SELECTOR_B({address_decode_1_special_memory_selector_b[15:4], SA_SHORT_PULSE_OUT_B, SA_FLAG_REGISTER_B, address_decode_1_special_memory_selector_b[1:0]}),
    .DEVICE_ADDRESS(DEVICE_ADDRESS), .KERNAL_ROM_B(KERNAL_ROM_B), .ADDRESS_IN_A0_24(ADDRESS),
    .DEVICE_VALID_B(DEVICE_VALID_B), .MAIN_MEMORY_VALID(MAIN_MEMORY_VALID), .RWB(RWB),
    .DEVICE_IDENTIFIER(DEVICE_IDENTIFIER), .KERNAL_MODE_B(pull_resistor_2_node),
    .INTERNAL_RAM_VALID(INTERNAL_MEMORY_VALID));
  Interrupt_Vectoring interrupt_vectoring_1 (
    .IRQ_3_B(not_5_out), .IRQ_1_B(not_3_out), .IRQ_4_B(not_6_out), .IRQ_5_B(not_7_out), .VPB(VPB),
    .IRQ_7_B(not_9_out), .NMI_B(NMI_B), .NMI_0_B(NMI_IN[0]), .NMI_1_B(NMI_IN[1]), .NMI_3_B(NMI_IN[3]),
    .IRQ_B(IRQ_B), .NMI_2_B(NMI_IN[2]), .ADDRESS_IN_A0_7(ADDRESS[7:0]), .IRQ_0_B(not_2_out),
    .IRQ_6_B(not_8_out), .IRQ_2_B(not_4_out), .ADDRESS_OUT_A0_7(IRAM_A0_7));
  // Probe on ADDRESS[15:0]
  Pull_Resistor #(.pull(1)) pull_resistor_4 (.node(microprocessor_w65c816_1_p15));
  // Probe on microprocessor_w65c816_1_p10
  LED led_9 (.in(INTERNAL_MEMORY_VALID));
  LED led_10 (.in(SPECIAL_ADDRESS_VALID_B));
  LED led_11 (.in(DEVICE_VALID_B));
  LED led_12 (.in(ROM_ADDRESS_VALID));
  LED led_13 (.in(MAIN_MEMORY_VALID));
  Pull_Resistor pull_resistor_5 (.node(ADDRESS[15:0]));
  // _8_bit_Bus_Transceiver__LVC4245 8_bit_bus_transceiver_lvc4245_1: pin names not known; wires that end beside it: DATA_TRANSMIT_B, microprocessor_w65c816_1_p10, RWB, D
  Signals signals_1 (
    .VDA(microprocessor_w65c816_1_p13), .RWB(RWB), .WRITE_SELECTOR(WRITE_SELECTOR),
    .CLOCK_ENABLE_B(CLOCK_ENABLE_B), .E(microprocessor_w65c816_1_p6), .NATIVE_MODE(NATIVE_MODE),
    .BANK_LATCH(BANK_LATCH), .READ_ENABLE_B(READ_ENABLE_B), .BA0_7(ADDRESS[23:16]),
    .WRITE_ENABLE(WRITE_ENABLE), .READ_SELECTOR(READ_SELECTOR), .READ_ENABLE(READ_ENABLE), .RWB_B(RWB_B),
    .D(microprocessor_w65c816_1_p10), .OPCODE_ADDRESS(OPCODE_ADDRESS), .WRITE_ENABLE_B(WRITE_ENABLE_B),
    .VPA(microprocessor_w65c816_1_p14));
  // Probe on ADDRESS
  Pull_Resistor pull_resistor_6 (.node(D));
  // Probe on D
  not not_10 (not_10_out, ROM_ADDRESS_VALID);
  // Probe on {ADDRESS[16:8], IRAM_A0_7}
  LED led_14 (.in(nand_1_out));
  LED led_15 (.in(nand_2_out));
  nand nand_1 (nand_1_out, INTERNAL_MEMORY_VALID, READ_ENABLE);
  nand nand_2 (nand_2_out, INTERNAL_MEMORY_VALID, WRITE_ENABLE);
  LED led_16 (.in(or_1_out));
  or or_1 (or_1_out, not_10_out, READ_ENABLE_B);
  RAM #(.\type ("nonvolatile"), .trigger("high"), .databus("bidir"), .addrWidth(17), .enables("line")) INTERNAL_MEMORY (
    .addr({ADDRESS[16:8], IRAM_A0_7}), .data(D));  // open: we, oe, clk
  // NOT_Gate not_11 has open pins: in=nand_1_out, out=open
  // NOT_Gate not_12 has open pins: in=nand_2_out, out=open
  // NOT_Gate not_13 has open pins: in=pull_resistor_7_node, out=open
  Pull_Resistor pull_resistor_7 (.node(pull_resistor_7_node));
  // Probe on {ADDRESS[14:8], IRAM_A0_7}
  ROM #(.addrWidth(16)) KERNAL_ROM (.addr({1'b1, ADDRESS[14:8], IRAM_A0_7}), .data(KERNAL_ROM_data));
  not not_14 (not_14_out, or_1_out);
  assign D = and_2_out ? D_IN : 8'bz;  // Controlled_Buffer controlled_buffer_1
  LED led_17 (.in(MAIN_MEMORY_VALID));
  and and_2 (and_2_out, MAIN_MEMORY_VALID, RWB);
  and and_3 (and_3_out, MAIN_MEMORY_VALID, RWB_B);
  Clock_Control clock_control_1 (
    .UNSTOPPABLE_CLOCK(STOP_SELECTOR), .CLOCK_ENABLE_B(CLOCK_ENABLE_B), .RESET(RESET),
    .ROM_ADDRESS_VALID(ROM_ADDRESS_VALID), .DEVICE_ADDRESS_VALID_B(DEVICE_VALID_B), .RWB_B(RWB_B));
  assign D_OUT = and_3_out ? D : 8'bz;  // Controlled_Buffer controlled_buffer_2
  assign D = not_14_out ? KERNAL_ROM_data : 8'bz;  // Controlled_Buffer controlled_buffer_3
  // Probe on D
  // Probe on D

  // Other names for the same wires on the sheet: IRQ_MPU0_2[2:0] = IRQ_OUT; RES_MPU0_2B[2:0] = RESB_OUT;
  //   A0_7[7:0] = ADDRESS[7:0]; A8_15[7:0] = ADDRESS[15:8]; BA0_7[7:0] = ADDRESS[23:16];
  //   DEVICE_ADDRESS_VALID_B = DEVICE_VALID_B; PULSE_0 = NMIB_OUT[0]; PULSE_1 = NMIB_OUT[1]; PULSE_2 = NMIB_OUT[2]

  // Notes on the sheet:
  //   contents of KERNAL_ROM (hex, n*v repeats v):
  //   16384*0 ad fc ff c9 2b e1 f0 2 0 0 e2 20 a9 a4 8d 0 70 a9 cc ad 0 70 1a 8d 0 70 a9 cc ad 0 70 c9 a5
  //   f0 2 0 0 a9 ff 8d 0 6f a9 2 8f 0 ff 1 a9 3 8f 1 ff 1 a9 0 48 a9 4 48 a9 1c 48 8 40 41194*ff 18 fb c2
  //   30 a9 ff 1 1b e2 20 a9 0 48 ab c2 20 5c 0 40 0 8b b c2 30 48 da 5a 80 2d 8b b c2 30 48 da 5a 80 24
  //   8b b c2 30 48 da 5a 80 1b 8b b c2 30 48 da 5a 80 12 8b b c2 30 48 da 5a 80 9 8b b c2 30 48 da 5a 80
  //   0 c2 30 7a fa 68 2b ab 40 7783*ff 5a e1 63 e1 51 e1 48 e1 0 0 3f e1 4*ff 6c e1 0 0 6c e1 6c e1 2b e1
  //   6c e1
  //   32KB_ROM
endmodule

module Timing_Circuit (
  input  RESET,
  output [7:0] SELECTOR,
  output RST,
  output RST_1,
  output CLK,
  output CLK_B,
  output HCLK,
  output HCLK_B,
  output [3:0] MULTIPLEXER,
  output [3:0] COUNTER,
  output RSTB
);

  wire clock_1_out, clock_2_out, digital_oscilloscope_1_p1, not_1_out, not_2_out, not_3_out, not_4_out,
       pull_resistor_1_node, pull_resistor_2_node, pull_resistor_3_node, pull_resistor_4_node,
       pull_resistor_5_node, pull_resistor_6_node, pull_resistor_8_node, pull_resistor_9_node;
  wire [3:0] pull_resistor_7_node;
  wire [7:2] n8_bit_serial_in_shift_lvc595_1_p6;
  wire [7:4] n8_bit_latch_lvc574_1_p4, n8_bit_latch_lvc574_1_p5;

  Clock clock_1 (.out(clock_1_out));
  not not_1 (not_1_out, RESET);
  Clock clock_2 (.out(clock_2_out));
  // EconoReset__DS1813 econoreset_ds1813_1: pin names not known; wires that end beside it: not_1_out, clock_2_out, RSTB
  // Digital_Oscilloscope #(.nState(32)) digital_oscilloscope_1: pin names not known; wires that end beside it: digital_oscilloscope_1_p1, SELECTOR[0], SELECTOR[1], SELECTOR[2], SELECTOR[3], SELECTOR[4], SELECTOR[5], SELECTOR[6], SELECTOR[7], RST, RST_1
  Clock clock_3 (.out(digital_oscilloscope_1_p1));
  Pull_Resistor pull_resistor_1 (.node(pull_resistor_1_node));
  D_Flip_Flop d_ff_1 (.clk(clock_1_out), .D(CLK_B), .Q(CLK), .Qn(CLK_B), .reset(not_2_out));  // open: preset
  not not_2 (not_2_out, RSTB);
  D_Flip_Flop d_ff_2 (.clk(CLK_B), .D(HCLK_B), .Q(HCLK), .Qn(HCLK_B), .reset(not_3_out));  // open: preset
  not not_3 (not_3_out, RSTB);
  // _8_bit_serial_in_shift__LVC595 8_bit_serial_in_shift_lvc595_1: pin names not known; wires that end beside it: pull_resistor_1_node, RSTB, RSTB, CLK, CLK, {n8_bit_serial_in_shift_lvc595_1_p6, RST_1, RST}
  Pull_Resistor #(.pull(1)) pull_resistor_2 (.node(pull_resistor_2_node));
  Pull_Resistor #(.pull(1)) pull_resistor_3 (.node(pull_resistor_3_node));
  Pull_Resistor #(.pull(1)) pull_resistor_4 (.node(pull_resistor_4_node));
  // _4_bit_Up_Counter__LVC163 4_bit_up_counter_lvc163_1: pin names not known; wires that end beside it: RST_1, pull_resistor_2_node, pull_resistor_3_node, CLK, pull_resistor_4_node, RST_1, COUNTER
  not not_4 (not_4_out, RST_1);
  Pull_Resistor #(.pull(1)) pull_resistor_5 (.node(pull_resistor_5_node));
  Pull_Resistor #(.pull(1)) pull_resistor_6 (.node(pull_resistor_6_node));
  // _2_to_4_Decoder__LVC139 2_to_4_decoder_lvc139_1: pin names not known; wires that end beside it: pull_resistor_5_node, not_4_out, pull_resistor_6_node, COUNTER[1:0], MULTIPLEXER
  Pull_Resistor #(.pull(1)) pull_resistor_7 (.node(pull_resistor_7_node));
  Pull_Resistor pull_resistor_8 (.node(pull_resistor_8_node));
  Pull_Resistor pull_resistor_9 (.node(pull_resistor_9_node));
  // _8_bit_Latch__LVC574 8_bit_latch_lvc574_1: pin names not known; wires that end beside it: pull_resistor_8_node, {pull_resistor_7_node, MULTIPLEXER}, CLK_B, {n8_bit_latch_lvc574_1_p4, SELECTOR[6], SELECTOR[4], SELECTOR[2], SELECTOR[0]}, n8_bit_latch_lvc574_1_p5[4], n8_bit_latch_lvc574_1_p4[4]
  // _8_bit_Latch__LVC574 8_bit_latch_lvc574_2: pin names not known; wires that end beside it: pull_resistor_9_node, {n8_bit_latch_lvc574_1_p4, SELECTOR[6], SELECTOR[4], SELECTOR[2], SELECTOR[0]}, CLK, {n8_bit_latch_lvc574_1_p5, SELECTOR[7], SELECTOR[5], SELECTOR[3], SELECTOR[1]}

  // Other names for the same wires on the sheet: RESET_0 = RST; RESET_1 = RST_1; CLOCK_B = CLK_B; HALF_CLOCK = HCLK;
  //   HALF_CLOCK_B = HCLK_B; SEL0 = SELECTOR[0]; SEL1 = SELECTOR[1]; SEL2 = SELECTOR[2]; SEL3 = SELECTOR[3];
  //   SEL4 = SELECTOR[4]; SEL5 = SELECTOR[5]; SEL6 = SELECTOR[6]; SEL7 = SELECTOR[7]

  // Notes on the sheet:
  //   Debug Outputs
endmodule

module Quick_Timing_Circuit (
  input  RESET,
  output [7:0] SELECTOR,
  output RST,
  output RST_1,
  output CLK,
  output CLK_B,
  output HCLK,
  output HCLK_B,
  output [3:0] MULTIPLEXER,
  output [3:0] COUNTER,
  output RSTB
);

  wire clock_2_out, not_1_out, not_3_out, not_4_out, pull_resistor_1_node, pull_resistor_2_node,
       pull_resistor_3_node, pull_resistor_4_node, pull_resistor_5_node, pull_resistor_6_node,
       pull_resistor_8_node, pull_resistor_9_node;
  wire [3:0] pull_resistor_7_node;
  wire [7:0] n8_bit_serial_in_shift_lvc595_1_p6;
  wire [7:4] n8_bit_latch_lvc574_1_p4, n8_bit_latch_lvc574_1_p5;

  Clock clock_1 (.out(CLK));
  not not_1 (not_1_out, RESET);
  D_Flip_Flop d_ff_1 (.clk(CLK), .D(not_1_out), .Q(RSTB));  // open: Qn, preset, reset
  Clock clock_2 (.out(clock_2_out));
  // Digital_Oscilloscope #(.nState(32)) digital_oscilloscope_1: pin names not known; wires that end beside it: clock_2_out, SELECTOR[0], SELECTOR[1], SELECTOR[2], SELECTOR[3], SELECTOR[4], SELECTOR[5], SELECTOR[6], SELECTOR[7], RST, RST_1
  Pull_Resistor pull_resistor_1 (.node(pull_resistor_1_node));
  not not_2 (CLK_B, CLK);
  D_Flip_Flop d_ff_2 (.clk(CLK), .D(HCLK_B), .Q(HCLK), .Qn(HCLK_B), .reset(not_3_out));  // open: preset
  not not_3 (not_3_out, RSTB);
  // _8_bit_serial_in_shift__LVC595 8_bit_serial_in_shift_lvc595_1: pin names not known; wires that end beside it: pull_resistor_1_node, RSTB, RSTB, CLK, CLK, {n8_bit_serial_in_shift_lvc595_1_p6[7:4], RST_1, n8_bit_serial_in_shift_lvc595_1_p6[2], RST, n8_bit_serial_in_shift_lvc595_1_p6[0]}
  Pull_Resistor #(.pull(1)) pull_resistor_2 (.node(pull_resistor_2_node));
  Pull_Resistor #(.pull(1)) pull_resistor_3 (.node(pull_resistor_3_node));
  Pull_Resistor #(.pull(1)) pull_resistor_4 (.node(pull_resistor_4_node));
  // _4_bit_Up_Counter__LVC163 4_bit_up_counter_lvc163_1: pin names not known; wires that end beside it: RST_1, pull_resistor_2_node, pull_resistor_3_node, CLK, pull_resistor_4_node, RST_1, COUNTER
  not not_4 (not_4_out, RST_1);
  Pull_Resistor #(.pull(1)) pull_resistor_5 (.node(pull_resistor_5_node));
  Pull_Resistor #(.pull(1)) pull_resistor_6 (.node(pull_resistor_6_node));
  // _2_to_4_Decoder__LVC139 2_to_4_decoder_lvc139_1: pin names not known; wires that end beside it: pull_resistor_5_node, not_4_out, pull_resistor_6_node, COUNTER[1:0], MULTIPLEXER
  Pull_Resistor #(.pull(1)) pull_resistor_7 (.node(pull_resistor_7_node));
  Pull_Resistor pull_resistor_8 (.node(pull_resistor_8_node));
  Pull_Resistor pull_resistor_9 (.node(pull_resistor_9_node));
  // _8_bit_Latch__LVC574 8_bit_latch_lvc574_1: pin names not known; wires that end beside it: pull_resistor_8_node, {pull_resistor_7_node, MULTIPLEXER}, CLK_B, {n8_bit_latch_lvc574_1_p4, SELECTOR[6], SELECTOR[4], SELECTOR[2], SELECTOR[0]}, n8_bit_latch_lvc574_1_p5[4], n8_bit_latch_lvc574_1_p4[4]
  // _8_bit_Latch__LVC574 8_bit_latch_lvc574_2: pin names not known; wires that end beside it: pull_resistor_9_node, {n8_bit_latch_lvc574_1_p4, SELECTOR[6], SELECTOR[4], SELECTOR[2], SELECTOR[0]}, CLK, {n8_bit_latch_lvc574_1_p5, SELECTOR[7], SELECTOR[5], SELECTOR[3], SELECTOR[1]}

  // Other names for the same wires on the sheet: RESET_0 = RST; RESET_1 = RST_1; CLOCK_B = CLK_B; HALF_CLOCK = HCLK;
  //   HALF_CLOCK_B = HCLK_B; SEL0 = SELECTOR[0]; SEL1 = SELECTOR[1]; SEL2 = SELECTOR[2]; SEL3 = SELECTOR[3];
  //   SEL4 = SELECTOR[4]; SEL5 = SELECTOR[5]; SEL6 = SELECTOR[6]; SEL7 = SELECTOR[7]

  // Notes on the sheet:
  //   Debug Outputs
endmodule

module Interrupt_Vectoring (
  input  [7:0] ADDRESS_IN_A0_7,
  input  VPB,
  input  IRQ_0_B,
  input  IRQ_1_B,
  input  IRQ_2_B,
  input  IRQ_3_B,
  input  IRQ_4_B,
  input  IRQ_5_B,
  input  IRQ_6_B,
  input  IRQ_7_B,
  input  NMI_0_B,
  input  NMI_1_B,
  input  NMI_2_B,
  input  NMI_3_B,
  output [7:0] ADDRESS_OUT_A0_7,
  output IRQ_B,
  output NMI_B
);

  wire n8_to_3_encoder_ls148_1_p4, n8_to_3_encoder_ls148_2_p4, nand_1_out, nand_2_out, not_1_out, not_2_out,
       not_3_out, not_4_out, pull_resistor_5_node, pull_resistor_6_node;
  wire [0:0] n8_bit_latch_lvc573_1_p4, n8_bit_latch_lvc573_2_p4, n8_bit_line_driver_lvc541_1_p4;
  wire [2:0] n8_to_3_encoder_ls148_1_p3, n8_to_3_encoder_ls148_2_p3;
  wire [3:0] pull_resistor_4_node;

  not not_1 (not_1_out, VPB);
  Pull_Resistor #(.pull(1)) pull_resistor_1 (.node(pull_resistor_4_node[3]));
  Pull_Resistor #(.pull(1)) pull_resistor_2 (.node(pull_resistor_4_node[2]));
  Pull_Resistor #(.pull(1)) pull_resistor_3 (.node(pull_resistor_4_node[1]));
  Pull_Resistor #(.pull(1)) pull_resistor_4 (.node(pull_resistor_4_node[0]));
  nand nand_1 (nand_1_out, ADDRESS_IN_A0_7[1], ADDRESS_IN_A0_7[2], ADDRESS_IN_A0_7[3], not_1_out);
  not not_2 (not_2_out, ADDRESS_IN_A0_7[2]);
  nand nand_2 (nand_2_out, ADDRESS_IN_A0_7[1], not_2_out, ADDRESS_IN_A0_7[3], not_1_out);
  not not_3 (not_3_out, nand_1_out);
  Pull_Resistor pull_resistor_5 (.node(pull_resistor_5_node));
  not not_4 (not_4_out, nand_2_out);
  Pull_Resistor pull_resistor_6 (.node(pull_resistor_6_node));
  // _8_to_3_Encoder__LS148 8_to_3_encoder_ls148_1: pin names not known; wires that end beside it: pull_resistor_5_node, {IRQ_0_B, IRQ_1_B, IRQ_2_B, IRQ_3_B, IRQ_4_B, IRQ_5_B, IRQ_6_B, IRQ_7_B}, n8_to_3_encoder_ls148_1_p3, n8_to_3_encoder_ls148_1_p4, IRQ_B
  // _8_to_3_Encoder__LS148 8_to_3_encoder_ls148_2: pin names not known; wires that end beside it: pull_resistor_6_node, {NMI_0_B, NMI_1_B, NMI_2_B, NMI_3_B, pull_resistor_4_node}, n8_to_3_encoder_ls148_2_p3, n8_to_3_encoder_ls148_2_p4, NMI_B
  // Probe on {4'b1101, n8_to_3_encoder_ls148_1_p3, 1'b0}
  // Probe on {4'b1100, n8_to_3_encoder_ls148_2_p3, 1'b0}
  // _8_bit_Line_Driver__LVC541 8_bit_line_driver_lvc541_1: pin names not known; wires that end beside it: not_3_out, not_4_out, ADDRESS_IN_A0_7, {ADDRESS_OUT_A0_7[7:1], n8_bit_line_driver_lvc541_1_p4[0]}
  // _8_bit_Latch__LVC573 8_bit_latch_lvc573_1: pin names not known; wires that end beside it: nand_1_out, {4'b1101, n8_to_3_encoder_ls148_1_p3, 1'b0}, n8_to_3_encoder_ls148_1_p4, {ADDRESS_OUT_A0_7[7:1], n8_bit_latch_lvc573_1_p4[0]}
  // _8_bit_Latch__LVC573 8_bit_latch_lvc573_2: pin names not known; wires that end beside it: nand_2_out, {4'b1100, n8_to_3_encoder_ls148_2_p3, 1'b0}, n8_to_3_encoder_ls148_2_p4, {ADDRESS_OUT_A0_7[7:1], n8_bit_latch_lvc573_2_p4[0]}

  assign ADDRESS_OUT_A0_7[0] = ADDRESS_IN_A0_7[0];

  // Notes on the sheet:
  //   Address A1..3 == %111 && !VPB
  //   ((Address == $XXXE || $XXXF) && VP)
  //   Address A1..3 == %101 && !VPB
  //   ((Address == $XXXA || $XXXB) && VP)
  //   Low byte of address if no interrupt vectoring is taking place
  //   Low byte of IRQ vector with high nybble set to $D and bit 0 set to 0
  //   Low byte of NMI vector with high nybble set to $C and bit 0 set to 0
  //   ($C0, $C2, $C4, $C6)
  //   ($D0, $D2, $D4, $D6, $D8, $DA, $DC or $DE)
endmodule

module Internal_Memory_Glue (
  input  [7:0] USER_BANK,
  input  [23:0] ADDRESS_IN_A0_23,
  input  INTERNAL_MEMORY_VALID,
  input  READ_ENABLE,
  input  READ_BANK_REMAP_B,
  input  WRITE_ENABLE,
  output [16:0] ADDRESS_OUT_A0_16,
  output OEB,
  output WEB,
  output CEB
);

  wire and_1_out, and_2_out, not_1_out, not_2_out, pull_resistor_1_node;

  Pull_Resistor #(.pull(1)) pull_resistor_1 (.node(pull_resistor_1_node));
  not not_1 (not_1_out, READ_BANK_REMAP_B);
  and and_1 (and_1_out, INTERNAL_MEMORY_VALID, READ_ENABLE);
  and and_2 (and_2_out, INTERNAL_MEMORY_VALID, WRITE_ENABLE);
  // _4_bit_Line_Driver__LVC125 4_bit_line_driver_lvc125_1: pin names not known; wires that end beside it: READ_BANK_REMAP_B, not_1_out, pull_resistor_1_node, pull_resistor_1_node, 1'b1, ADDRESS_IN_A0_23[16], ADDRESS_OUT_A0_16[16], ADDRESS_OUT_A0_16[16]
  // _16_bit_Line_Driver__LVC16244 16_bit_line_driver_lvc16244_1: pin names not known; wires that end beside it: READ_BANK_REMAP_B, READ_BANK_REMAP_B, READ_BANK_REMAP_B, READ_BANK_REMAP_B, USER_BANK[7:4], USER_BANK[3:0], ADDRESS_IN_A0_23[23:20], ADDRESS_IN_A0_23[19:16], ADDRESS_OUT_A0_16[15:12], ADDRESS_OUT_A0_16[11:8], ADDRESS_OUT_A0_16[7:4], ADDRESS_OUT_A0_16[3:0]
  // _16_bit_Line_Driver__LVC16244 16_bit_line_driver_lvc16244_2: pin names not known; wires that end beside it: not_1_out, not_1_out, not_1_out, not_1_out, ADDRESS_IN_A0_23[15:12], ADDRESS_IN_A0_23[11:8], ADDRESS_IN_A0_23[7:4], ADDRESS_IN_A0_23[3:0], ADDRESS_OUT_A0_16[15:12], ADDRESS_OUT_A0_16[11:8], ADDRESS_OUT_A0_16[7:4], ADDRESS_OUT_A0_16[3:0]
  not not_2 (not_2_out, READ_BANK_REMAP_B);
  nor nor_1 (OEB, and_1_out, not_2_out);
  nand nand_1 (WEB, READ_BANK_REMAP_B, and_2_out);
  Pull_Resistor pull_resistor_2 (.node(CEB));
endmodule

module Address_Decode (
  input  [23:0] ADDRESS_IN_A0_24,
  input  KERNAL_ROM_B,
  input  RWB,
  input  KERNAL_MODE,
  input  KERNAL_MODE_B,
  output INTERNAL_RAM_VALID,
  output SPECIAL_VALID_B,
  output DEVICE_VALID_B,
  output ROM_VALID,
  output MAIN_MEMORY_VALID,
  output [1:0] DEVICE_CHANNEL,
  output [5:0] DEVICE_IDENTIFIER,
  output [3:0] DEVICE_ADDRESS,
  output [15:0] SPECIAL_MEMORY_SELECTOR_B
);

  wire and_1_out, and_2_out, and_3_out, and_4_out, and_5_out, and_6_out, and_7_out, and_8_out, and_10_out,
       n8_bit_comparator_f521_1_p4, nand_1_out, nand_2_out, nand_3_out, not_1_out, not_2_out, not_3_out,
       not_4_out, not_5_out, not_6_out, not_7_out, not_8_out, not_9_out, not_10_out, not_11_out, not_12_out,
       not_13_out, not_14_out, or_1_out, pull_resistor_1_node, pull_resistor_2_node;

  Pull_Resistor pull_resistor_1 (.node(pull_resistor_1_node));
  not not_1 (not_1_out, ADDRESS_IN_A0_24[16]);
  not not_2 (not_2_out, ADDRESS_IN_A0_24[17]);
  not not_3 (not_3_out, ADDRESS_IN_A0_24[18]);
  not not_4 (not_4_out, ADDRESS_IN_A0_24[19]);
  not not_5 (not_5_out, ADDRESS_IN_A0_24[20]);
  not not_6 (not_6_out, ADDRESS_IN_A0_24[21]);
  not not_7 (not_7_out, ADDRESS_IN_A0_24[22]);
  not not_8 (not_8_out, ADDRESS_IN_A0_24[23]);
  Pull_Resistor #(.pull(1)) pull_resistor_2 (.node(pull_resistor_2_node));
  not not_9 (not_9_out, KERNAL_ROM_B);
  not not_10 (not_10_out, ADDRESS_IN_A0_24[15]);
  // _8_bit_Comparator__F521 8_bit_comparator_f521_1: pin names not known; wires that end beside it: pull_resistor_1_node, ADDRESS_IN_A0_24[15:8], 8'h6f, n8_bit_comparator_f521_1_p4
  not not_11 (not_11_out, ADDRESS_IN_A0_24[3]);
  and and_1 (and_1_out, not_1_out, not_2_out, not_3_out, not_4_out);
  and and_2 (and_2_out, not_5_out, not_6_out, not_7_out, not_8_out);
  and and_3 (and_3_out, not_4_out, not_3_out, not_2_out, pull_resistor_2_node);
  and and_4 (and_4_out, ADDRESS_IN_A0_24[15], not_9_out, RWB);
  and and_5 (and_5_out, ADDRESS_IN_A0_24[12], ADDRESS_IN_A0_24[13], ADDRESS_IN_A0_24[14], not_10_out);
  not not_12 (not_12_out, and_2_out);
  not not_13 (not_13_out, and_1_out);
  and and_6 (and_6_out, and_2_out, and_1_out);
  and and_7 (and_7_out, and_3_out, and_2_out);
  nand nand_1 (nand_1_out, and_3_out, and_2_out);
  not not_14 (not_14_out, and_5_out);
  nand nand_2 (nand_2_out, and_5_out, and_1_out, and_2_out);
  or or_1 (or_1_out, not_12_out, not_13_out, n8_bit_comparator_f521_1_p4);
  and and_8 (and_8_out, and_1_out, and_2_out, KERNAL_MODE);
  nand nand_3 (nand_3_out, and_6_out, and_4_out);
  and and_9 (ROM_VALID, and_6_out, KERNAL_MODE, and_4_out);
  and and_10 (and_10_out, not_14_out, n8_bit_comparator_f521_1_p4);
  or or_2 (MAIN_MEMORY_VALID, nand_1_out, KERNAL_MODE_B);
  or or_3 (DEVICE_VALID_B, KERNAL_MODE_B, nand_2_out);
  or or_4 (SPECIAL_VALID_B, KERNAL_MODE_B, or_1_out);
  // _3_to_8_Decoder__LVC138 3_to_8_decoder_lvc138_1: pin names not known; wires that end beside it: n8_bit_comparator_f521_1_p4, not_11_out, ADDRESS_IN_A0_24[2:0], and_8_out, SPECIAL_MEMORY_SELECTOR_B[15:8]
  // _3_to_8_Decoder__LVC138 3_to_8_decoder_lvc138_2: pin names not known; wires that end beside it: n8_bit_comparator_f521_1_p4, ADDRESS_IN_A0_24[3], ADDRESS_IN_A0_24[2:0], and_8_out, SPECIAL_MEMORY_SELECTOR_B[7:0]
  and and_11 (INTERNAL_RAM_VALID, and_7_out, KERNAL_MODE, nand_3_out, and_10_out);
  LED led_1 (.in(INTERNAL_RAM_VALID));
  LED led_2 (.in(SPECIAL_VALID_B));
  LED led_3 (.in(DEVICE_VALID_B));
  LED led_4 (.in(ROM_VALID));
  LED led_5 (.in(MAIN_MEMORY_VALID));

  assign DEVICE_ADDRESS = ADDRESS_IN_A0_24[11:8];
  assign DEVICE_CHANNEL = ADDRESS_IN_A0_24[7:6];
  assign DEVICE_IDENTIFIER = ADDRESS_IN_A0_24[5:0];

  // Notes on the sheet:
  //   Bank Decode
  //   ROM Decode
  //   Device Decode (7000 to 7FFF)
  //   Address A12..15 == $F
  //   Special Memory Decode (7700 to 770F) repeats (7710 to 77FF)
  //   bits 0..3 all zero
  //   bits 4..7 all zero
  //   bits 1..3 all zero
  //   bank zero
  //   bank zero or one
  //   !(bank zero or one)
  //   !(bank zero && device address)
  //   !(kernal mode) || !(bank zero or one)
endmodule

module Interrupt_Detection (
  input  NATIVE_MODE,
  input  ADDRESS_IN_A0,
  input  PHI2_B,
  input  OPCODE_ADDRESS,
  input  [7:0] D,
  input  RESET_B,
  input  LATCH_D,
  output ENTER_INTERRUPT,
  output [7:0] OPCODE,
  output RETURN_FROM_INTERRUPT
);

  wire and_1_out, and_2_out, and_3_out, and_4_out, d_ff_1_q, d_ff_2_q, d_ff_2_qn,
       n8_bit_comparator_f521_1_p4, n8_bit_comparator_f521_2_p4, n8_bit_comparator_f521_3_p4, nand_1_out,
       nor_1_out, not_1_out, not_2_out, not_3_out, not_4_out, not_5_out, or_1_out, pull_resistor_2_node,
       pull_resistor_3_node, pull_resistor_4_node, pull_resistor_5_node, xor_1_out;
  wire [7:0] n8_bit_serial_in_shift_lvc595_1_p6;

  not not_1 (not_1_out, RESET_B);
  not not_2 (not_2_out, OPCODE_ADDRESS);
  not not_3 (not_3_out, RESET_B);
  Pull_Resistor pull_resistor_1 ();  // open: node
  and and_1 (and_1_out, OPCODE_ADDRESS, LATCH_D);
  xor xor_1 (xor_1_out, ADDRESS_IN_A0, d_ff_1_q);
  D_Flip_Flop d_ff_1 (.clk(PHI2_B), .D(ADDRESS_IN_A0), .Q(d_ff_1_q), .reset(not_1_out));  // open: Qn, preset
  D_Flip_Flop d_ff_2 (.clk(PHI2_B), .D(not_2_out), .Q(d_ff_2_q), .Qn(d_ff_2_qn), .reset(not_3_out));  // open: preset
  // _8_bit_Latch__LVC573 8_bit_latch_lvc573_1: pin names not known; wires that end beside it: D, and_1_out, OPCODE
  nor nor_1 (nor_1_out, xor_1_out, d_ff_2_q);
  Pull_Resistor pull_resistor_2 (.node(pull_resistor_2_node));
  Pull_Resistor pull_resistor_3 (.node(pull_resistor_3_node));
  Pull_Resistor pull_resistor_4 (.node(pull_resistor_4_node));
  // _8_bit_Comparator__F521 8_bit_comparator_f521_1: pin names not known; wires that end beside it: pull_resistor_2_node, OPCODE, {8{1'b0}}, n8_bit_comparator_f521_1_p4
  // _8_bit_Comparator__F521 8_bit_comparator_f521_2: pin names not known; wires that end beside it: pull_resistor_3_node, OPCODE, 8'h2, n8_bit_comparator_f521_2_p4
  // _8_bit_Comparator__F521 8_bit_comparator_f521_3: pin names not known; wires that end beside it: pull_resistor_4_node, OPCODE, 8'h40, n8_bit_comparator_f521_3_p4
  nand nand_1 (nand_1_out, n8_bit_comparator_f521_1_p4, n8_bit_comparator_f521_2_p4);
  not not_4 (not_4_out, n8_bit_comparator_f521_3_p4);
  and and_2 (and_2_out, xor_1_out, d_ff_2_qn, nand_1_out);
  and and_3 (and_3_out, xor_1_out, d_ff_2_qn, not_4_out);
  or or_1 (or_1_out, nor_1_out, and_2_out);
  Pull_Resistor pull_resistor_5 (.node(pull_resistor_5_node));
  not not_5 (not_5_out, RESET_B);
  // _8_bit_serial_in_shift__LVC595 8_bit_serial_in_shift_lvc595_1: pin names not known; wires that end beside it: pull_resistor_5_node, RESET_B, and_3_out, LATCH_D, LATCH_D, n8_bit_serial_in_shift_lvc595_1_p6
  and and_4 (and_4_out, NATIVE_MODE, LATCH_D, or_1_out);
  and and_5 (RETURN_FROM_INTERRUPT, NATIVE_MODE, LATCH_D, n8_bit_serial_in_shift_lvc595_1_p6[4]);
  or or_2 (ENTER_INTERRUPT, not_5_out, and_4_out);
  // Probe on OPCODE
  // Probe on n8_bit_serial_in_shift_lvc595_1_p6

  // Notes on the sheet:
  //   BRK
  //   COP
  //   RTI
endmodule

module Kernal_User_Mode (
  input  SA_USER_PROGRAM_ID_B,
  input  SA_INTERRUPTS_IN_DEPTH_B,
  input  READ_ENABLE_B,
  input  WRITE_ENABLE_B,
  input  RESET,
  input  [7:0] D_IN,
  input  ENTER_INTERRUPT,
  input  EXIT_INTERRUPT,
  output [7:0] USER,
  output [7:0] D_OUT,
  output KERNAL_MODE2,
  output KERNAL_MODE_B2,
  output [7:0] INTERRUPT_DEPTH
);

  wire n4_bit_up_down_counter_hct193_1_p4, n4_bit_up_down_counter_hct193_1_p5, nor_1_out, not_1_out,
       not_2_out, not_3_out, or_1_out, or_2_out, or_3_out, pull_resistor_1_node, pull_resistor_2_node;

  not not_1 (not_1_out, RESET);
  nor nor_1 (nor_1_out, WRITE_ENABLE_B, SA_USER_PROGRAM_ID_B);
  or or_1 (or_1_out, SA_USER_PROGRAM_ID_B, READ_ENABLE_B);
  or or_2 (or_2_out, READ_ENABLE_B, SA_INTERRUPTS_IN_DEPTH_B);
  or or_3 (or_3_out, SA_INTERRUPTS_IN_DEPTH_B, WRITE_ENABLE_B);
  not not_2 (not_2_out, ENTER_INTERRUPT);
  not not_3 (not_3_out, EXIT_INTERRUPT);
  Pull_Resistor pull_resistor_1 (.node(pull_resistor_1_node));
  // _8_bit_Latch__LVC573 8_bit_latch_lvc573_1: pin names not known; wires that end beside it: pull_resistor_1_node, D_IN, nor_1_out, USER
  // _4_bit_Up_Down_Counter__HCT193 4_bit_up_down_counter_hct193_1: pin names not known; wires that end beside it: or_3_out, not_1_out, D_IN[7:4], n4_bit_up_down_counter_hct193_1_p4, n4_bit_up_down_counter_hct193_1_p5, INTERRUPT_DEPTH[7:4]
  // _4_bit_Up_Down_Counter__HCT193 4_bit_up_down_counter_hct193_2: pin names not known; wires that end beside it: or_3_out, not_1_out, D_IN[3:0], not_2_out, not_3_out, INTERRUPT_DEPTH[3:0], n4_bit_up_down_counter_hct193_1_p4, n4_bit_up_down_counter_hct193_1_p5
  // Probe on USER
  Pull_Resistor pull_resistor_2 (.node(pull_resistor_2_node));
  // Probe on INTERRUPT_DEPTH
  // _16_bit_Line_Driver__LVC16244 16_bit_line_driver_lvc16244_1: pin names not known; wires that end beside it: or_1_out, or_1_out, or_2_out, or_2_out, USER[7:4], USER[3:0], INTERRUPT_DEPTH[7:4], INTERRUPT_DEPTH[3:0], D_OUT[7:4], D_OUT[3:0], D_OUT[7:4], D_OUT[3:0]
  // _8_bit_Comparator__F521 8_bit_comparator_f521_1: pin names not known; wires that end beside it: pull_resistor_2_node, {8{1'b0}}, INTERRUPT_DEPTH, KERNAL_MODE2
  // Probe on KERNAL_MODE2
  not not_4 (KERNAL_MODE_B2, KERNAL_MODE2);

  // Notes on the sheet:
  //   User Program
  //   Interrupt Depth
endmodule

module Flags_And_Pulse (
  input  SA_FLAG_REGISTER_B,
  input  SA_SHORT_PULSE_OUT_B,
  input  RESET,
  input  WRITE_ENABLE_B,
  input  READ_ENABLE_B,
  input  PHI2,
  input  [7:0] D_IN,
  output [7:0] FLAG_REGISTER,
  output [7:0] D_OUT,
  output PULSE_0,
  output PULSE_1,
  output PULSE_2
);

  wire d_ff_1_q, d_ff_2_qn, d_ff_3_q, d_ff_4_qn, d_ff_5_q, d_ff_6_qn, nor_1_out, nor_2_out, nor_3_out,
       nor_4_out, not_1_out, not_2_out, not_3_out, not_4_out, not_5_out, not_6_out, not_7_out, not_8_out,
       not_9_out, or_1_out, or_2_out, pull_resistor_1_node, pull_resistor_2_node, pull_resistor_3_node;

  or or_1 (or_1_out, READ_ENABLE_B, SA_FLAG_REGISTER_B);
  or or_2 (or_2_out, SA_SHORT_PULSE_OUT_B, READ_ENABLE_B);
  not not_1 (not_1_out, D_IN[0]);
  not not_2 (not_2_out, D_IN[1]);
  not not_3 (not_3_out, D_IN[2]);
  nor nor_1 (nor_1_out, SA_SHORT_PULSE_OUT_B, not_3_out, WRITE_ENABLE_B);
  D_Flip_Flop d_ff_1 (.clk(nor_1_out), .D(pull_resistor_1_node), .Q(d_ff_1_q), .reset(not_4_out));  // open: Qn, preset
  Pull_Resistor #(.pull(1)) pull_resistor_1 (.node(pull_resistor_1_node));
  not not_4 (not_4_out, d_ff_2_qn);
  D_Flip_Flop d_ff_2 (.clk(PHI2), .D(d_ff_1_q), .Q(PULSE_2), .Qn(d_ff_2_qn), .reset(not_5_out));  // open: preset
  not not_5 (not_5_out, RESET);
  nor nor_2 (nor_2_out, SA_FLAG_REGISTER_B, WRITE_ENABLE_B);
  nor nor_3 (nor_3_out, not_2_out, SA_SHORT_PULSE_OUT_B, WRITE_ENABLE_B);
  D_Flip_Flop d_ff_3 (.clk(nor_3_out), .D(pull_resistor_2_node), .Q(d_ff_3_q), .reset(not_6_out));  // open: Qn, preset
  Pull_Resistor #(.pull(1)) pull_resistor_2 (.node(pull_resistor_2_node));
  not not_6 (not_6_out, d_ff_4_qn);
  D_Flip_Flop d_ff_4 (.clk(PHI2), .D(d_ff_3_q), .Q(PULSE_1), .Qn(d_ff_4_qn), .reset(not_7_out));  // open: preset
  not not_7 (not_7_out, RESET);
  // _8_bit_Latch__LVC273 8_bit_latch_lvc273_1: pin names not known; wires that end beside it: RESET, D_IN, nor_2_out, FLAG_REGISTER
  nor nor_4 (nor_4_out, not_1_out, SA_SHORT_PULSE_OUT_B, WRITE_ENABLE_B);
  Pull_Resistor #(.pull(1)) pull_resistor_3 (.node(pull_resistor_3_node));
  D_Flip_Flop d_ff_5 (.clk(nor_4_out), .D(pull_resistor_3_node), .Q(d_ff_5_q), .reset(not_8_out));  // open: Qn, preset
  not not_8 (not_8_out, d_ff_6_qn);
  D_Flip_Flop d_ff_6 (.clk(PHI2), .D(d_ff_5_q), .Q(PULSE_0), .Qn(d_ff_6_qn), .reset(not_9_out));  // open: preset
  not not_9 (not_9_out, RESET);
  // _16_bit_Line_Driver__LVC16244 16_bit_line_driver_lvc16244_1: pin names not known; wires that end beside it: or_1_out, or_1_out, or_2_out, or_2_out, FLAG_REGISTER[7:4], FLAG_REGISTER[3:0], D_OUT[7:4], D_OUT[3:0], D_OUT[7:4], D_OUT[3:0]
  // Probe on FLAG_REGISTER
endmodule

module Clock_Control (
  input  RWB_B,
  input  ROM_ADDRESS_VALID,
  input  DEVICE_ADDRESS_VALID_B,
  input  UNSTOPPABLE_CLOCK,
  input  RESET,
  output CLOCK_ENABLE_B
);

  wire and_1_out, and_2_out, and_3_out, d_ff_2_q, d_ff_2_qn, d_ff_3_qn, nor_1_out, not_1_out, not_2_out,
       not_3_out, not_4_out, or_1_out, or_2_out;

  not not_1 (not_1_out, ROM_ADDRESS_VALID);
  and and_1 (and_1_out, not_1_out, DEVICE_ADDRESS_VALID_B);
  nor nor_1 (nor_1_out, RWB_B, and_1_out);
  and and_2 (and_2_out, RESET, or_1_out, or_2_out);
  or or_1 (or_1_out, not_1_out, d_ff_2_qn);
  D_Flip_Flop d_ff_1 (
    .clk(UNSTOPPABLE_CLOCK), .D(nor_1_out), .Q(CLOCK_ENABLE_B), .reset(not_2_out));  // open: Qn, preset
  not not_2 (not_2_out, and_2_out);
  or or_2 (or_2_out, DEVICE_ADDRESS_VALID_B, d_ff_3_qn);
  and and_3 (and_3_out, RESET, CLOCK_ENABLE_B);
  D_Flip_Flop d_ff_2 (
    .clk(UNSTOPPABLE_CLOCK), .D(CLOCK_ENABLE_B), .Q(d_ff_2_q), .Qn(d_ff_2_qn), .reset(not_3_out));  // open: preset
  not not_3 (not_3_out, and_3_out);
  D_Flip_Flop d_ff_3 (.clk(UNSTOPPABLE_CLOCK), .D(d_ff_2_q), .Qn(d_ff_3_qn), .reset(not_4_out));  // open: Q, preset
  not not_4 (not_4_out, and_3_out);
endmodule

module Selector_State (
  input  CLOCK_ENABLE_B,
  input  [7:0] SELECTOR,
  input  RESET,
  output SEL0,
  output BANK_LATCH,
  output SEL1,
  output DATA_TRANSMIT_B,
  output SEL2,
  output READ_BANK_REMAP_B,
  output SEL3,
  output STOP_SELECTOR,
  output SEL4,
  output SEL5,
  output WRITE_SELECTOR,
  output MRAM_ACCESS_B,
  output SEL6,
  output READ_SELECTOR,
  output SEL7,
  output PHI2,
  output BOARD_RESET
);

  wire pull_resistor_1_node;
  wire [7:0] n8_bit_serial_in_shift_lvc595_1_p6;

  Pull_Resistor pull_resistor_1 (.node(pull_resistor_1_node));
  or or_1 (SEL0, CLOCK_ENABLE_B, SELECTOR[0]);
  or or_2 (SEL1, CLOCK_ENABLE_B, SELECTOR[1]);
  or or_3 (READ_BANK_REMAP_B, CLOCK_ENABLE_B, SELECTOR[2]);
  or or_4 (SEL3, CLOCK_ENABLE_B, SELECTOR[3]);
  or or_5 (SEL4, CLOCK_ENABLE_B, SELECTOR[4]);
  or or_6 (SEL5, CLOCK_ENABLE_B, SELECTOR[5]);
  or or_7 (MRAM_ACCESS_B, CLOCK_ENABLE_B, SELECTOR[6]);
  or or_8 (SEL7, CLOCK_ENABLE_B, SELECTOR[7]);
  // _8_bit_serial_in_shift__LVC595 8_bit_serial_in_shift_lvc595_1: pin names not known; wires that end beside it: pull_resistor_1_node, RESET, RESET, SELECTOR[3], SELECTOR[3], {n8_bit_serial_in_shift_lvc595_1_p6[7:4], BOARD_RESET, n8_bit_serial_in_shift_lvc595_1_p6[2:0]}
  not not_1 (BANK_LATCH, SEL1);
  nand nand_1 (DATA_TRANSMIT_B, SEL1, READ_BANK_REMAP_B);
  nand nand_2 (WRITE_SELECTOR, SEL5, MRAM_ACCESS_B);
  nand nand_3 (READ_SELECTOR, SEL5, MRAM_ACCESS_B, SEL7);
  and and_1 (PHI2, SEL0, n8_bit_serial_in_shift_lvc595_1_p6[0]);

  assign SEL2 = READ_BANK_REMAP_B;
  assign SEL6 = MRAM_ACCESS_B;
  assign STOP_SELECTOR = SELECTOR[3];
endmodule

module Signals (
  input  [7:0] D,
  input  RWB,
  input  VDA,
  input  VPA,
  input  E,
  input  READ_SELECTOR,
  input  WRITE_SELECTOR,
  input  CLOCK_ENABLE_B,
  input  BANK_LATCH,
  output [7:0] BA0_7,
  output NATIVE_MODE,
  output RWB_B,
  output WRITE_ENABLE,
  output WRITE_ENABLE_B,
  output READ_ENABLE,
  output READ_ENABLE_B,
  output OPCODE_ADDRESS
);

  wire or_1_out, or_2_out, pull_resistor_1_node;

  // Probe on D
  not not_1 (RWB_B, RWB);
  Pull_Resistor pull_resistor_1 (.node(pull_resistor_1_node));
  and and_1 (OPCODE_ADDRESS, VDA, VPA);
  or or_1 (or_1_out, VDA, VPA);
  // _8_bit_Latch__LVC573 8_bit_latch_lvc573_1: pin names not known; wires that end beside it: pull_resistor_1_node, D, BANK_LATCH, BA0_7
  not not_2 (NATIVE_MODE, E);
  and and_2 (WRITE_ENABLE, WRITE_SELECTOR, RWB_B, or_1_out);
  and and_3 (READ_ENABLE, RWB, or_1_out, or_2_out);
  or or_2 (or_2_out, READ_SELECTOR, CLOCK_ENABLE_B);
  not not_3 (WRITE_ENABLE_B, WRITE_ENABLE);
  not not_4 (READ_ENABLE_B, READ_ENABLE);
endmodule

module Gateway_Latch (
  input  LEAB,
  input  OEBA,
  input  ACCESS_SELECTOR_B,
  input  OEAB,
  input  TRANSFER_ENABLE,
  input  [7:0] D_IN,
  input  [7:0] XD_IN,
  input  RDY,
  input  [23:0] ADDRESS_IN_A0_23,
  output [7:0] D_OUT,
  output [7:0] XD_OUT,
  output MREAD,
  output MWRITE,
  output MVALID,
  output MREADY,
  output [23:0] MADDRESS_OUT_A0_23
);

  wire n8_bit_bi_latch_lvc543_1_p8, not_2_out, or_1_out, or_2_out, pull_resistor_1_node, pull_resistor_2_node;
  wire [1:1] not_1_out;
  wire [7:0] controlled_buffer_1_out, n8_bit_bi_latch_lvc543_1_p5;

  not not_1 (not_1_out[1], LEAB);
  assign controlled_buffer_1_out = LEAB ? D_IN : 8'bz;  // Controlled_Buffer controlled_buffer_1
  assign D_OUT = not_1_out[1] ? controlled_buffer_1_out : 8'bz;  // Controlled_Buffer controlled_buffer_2
  not not_2 (not_2_out, TRANSFER_ENABLE);
  // Probe on controlled_buffer_1_out
  or or_1 (or_1_out, OEBA, ACCESS_SELECTOR_B, not_2_out);
  or or_2 (or_2_out, OEAB, ACCESS_SELECTOR_B, not_2_out);
  Pull_Resistor pull_resistor_1 (.node(pull_resistor_1_node));
  Pull_Resistor #(.pull(1)) pull_resistor_2 (.node(pull_resistor_2_node));
  // _8_bit_Bi_latch__LVC543 8_bit_bi_latch_lvc543_1: pin names not known; wires that end beside it: LEAB, or_2_out, pull_resistor_1_node, controlled_buffer_1_out, n8_bit_bi_latch_lvc543_1_p5, not_1_out[1], or_1_out, n8_bit_bi_latch_lvc543_1_p8
  // _16_bit_Line_Driver__LVC16244 16_bit_line_driver_lvc16244_1: pin names not known; wires that end beside it: pull_resistor_2_node, ACCESS_SELECTOR_B, ACCESS_SELECTOR_B, ACCESS_SELECTOR_B, {RDY, TRANSFER_ENABLE, not_1_out[1], LEAB}, ADDRESS_IN_A0_23[19:16], ADDRESS_IN_A0_23[23:20], {MREADY, MVALID, MWRITE, MREAD}, MADDRESS_OUT_A0_23[19:16], MADDRESS_OUT_A0_23[23:20]
  // _16_bit_Line_Driver__LVC16244 16_bit_line_driver_lvc16244_2: pin names not known; wires that end beside it: ACCESS_SELECTOR_B, ACCESS_SELECTOR_B, ACCESS_SELECTOR_B, ACCESS_SELECTOR_B, ADDRESS_IN_A0_23[15:12], ADDRESS_IN_A0_23[11:8], ADDRESS_IN_A0_23[7:4], ADDRESS_IN_A0_23[3:0], MADDRESS_OUT_A0_23[15:12], MADDRESS_OUT_A0_23[11:8], MADDRESS_OUT_A0_23[7:4], MADDRESS_OUT_A0_23[3:0]
  Pull_Resistor pull_resistor_3 (.node(n8_bit_bi_latch_lvc543_1_p8));
  assign n8_bit_bi_latch_lvc543_1_p5 = LEAB ? XD_IN : 8'bz;  // Controlled_Buffer controlled_buffer_3
  assign XD_OUT = not_1_out[1] ? n8_bit_bi_latch_lvc543_1_p5 : 8'bz;  // Controlled_Buffer controlled_buffer_4
  Pull_Resistor pull_resistor_4 (.node(MREAD));
  Pull_Resistor pull_resistor_5 (.node(MWRITE));
  Pull_Resistor pull_resistor_6 (.node(MVALID));
  Pull_Resistor pull_resistor_7 (.node(MREADY));
  // Probe on MADDRESS_OUT_A0_23
  Pull_Resistor pull_resistor_8 (.node(MADDRESS_OUT_A0_23));
endmodule

module Device_Bus (
  input  MPU_0_RWB,
  input  [7:0] MPU_0_D_IN,
  input  [7:0] CH_0_D_IN,
  input  [5:0] MPU_0_DEVICE_IDENTIFIER,
  input  FST,
  input  [3:0] MPU_0_DEVICE_ADDRESS,
  input  SEL_4,
  input  SEL_6,
  input  MPU_0_DEVICE_VALID_B,
  input  SEL_0,
  input  [1:0] MPU_0_DEVICE_CHANNEL,
  input  SEL_2,
  input  [1:0] MPU_1_DEVICE_CHANNEL,
  input  MPU_1_DEVICE_VALID_B,
  input  MPU_1_RWB,
  input  [7:0] MPU_1_D_IN,
  input  [7:0] CH_1_D_IN,
  input  [5:0] MPU_1_DEVICE_IDENTIFIER,
  input  [3:0] MPU_1_DEVICE_ADDRESS,
  input  MPU_2_RWB,
  input  [7:0] MPU_2_D_IN,
  input  [7:0] CH_2_D_IN,
  input  [5:0] MPU_2_DEVICE_IDENTIFIER,
  input  [3:0] MPU_2_DEVICE_ADDRESS,
  input  MPU_2_DEVICE_VALID,
  input  [1:0] MPU_2_DEVICE_CHANNEL,
  input  [1:0] MPU_3_DEVICE_CHANNEL,
  input  MPU_3_DEVICE_VALID,
  input  MPU_3_RWB,
  input  [7:0] MPU_3_D_IN,
  input  [7:0] CH_3_D_IN,
  input  [5:0] MPU_3_DEVICE_IDENTIFIER,
  input  [3:0] MPU_3_DEVICE_ADDRESS,
  output [7:0] MPU_0_D_OUT,
  output [7:0] CH_0_D_OUT,
  output [5:0] CH_0_DEVICE_IDENTIFIER,
  output [3:0] CH_0_DEVICE_ADDRESS,
  output CH_0_RWB_B,
  output CH_0_RWB,
  output CH_0_DEVICE_VALID_B,
  output [7:0] MPU_1_D_OUT,
  output [7:0] CH_1_D_OUT,
  output [5:0] CH_1_DEVICE_IDENTIFIER,
  output [3:0] CH_1_DEVICE_ADDRESS,
  output CH_1_RWB_B,
  output CH_1_RWB,
  output CH_1_DEVICE_VALID_B,
  output [7:0] MPU_2_D_OUT,
  output [7:0] CH_2_D_OUT,
  output [5:0] CH_2_DEVICE_IDENTIFIER,
  output [3:0] CH_2_DEVICE_ADDRESS,
  output CH_2_RWB_B,
  output CH_2_RWB,
  output CH_2_DEVICE_VALID_B,
  output [7:0] MPU_3_D_OUT,
  output [7:0] CH_3_D_OUT,
  output [5:0] CH_3_DEVICE_IDENTIFIER,
  output [3:0] CH_3_DEVICE_ADDRESS,
  output CH_3_RWB_B,
  output CH_3_RWB,
  output CH_3_DEVICE_VALID_B
);

  wire and_1_out, and_2_out, and_3_out, and_4_out, and_5_out, and_6_out, and_7_out, and_8_out, and_9_out,
       and_10_out, and_11_out, and_12_out, d_ff_1_q, d_ff_2_q, d_ff_3_q, d_ff_4_q, decoder_1_out0,
       decoder_1_out1, decoder_1_out2, decoder_1_out3, FST_t, MPU_0_DEVICE_VALID, MPU_0_RWB_B,
       MPU_1_DEVICE_VALID, MPU_1_RWB_B, MPU_2_DEVICE_VALID_t, MPU_2_RWB_B, MPU_3_DEVICE_VALID_t, MPU_3_RWB_B,
       n4_bit_line_driver_lvc125_1_p9, n4_bit_line_driver_lvc125_1_p10, n4_bit_line_driver_lvc125_1_p11,
       n4_bit_line_driver_lvc125_1_p12, n8_bit_bi_latch_lvc543_1_p5, nor_1_out, nor_2_out, nor_3_out,
       nor_4_out, or_1_out, or_2_out, or_3_out, or_4_out, or_5_out, or_6_out, or_7_out, or_8_out, or_9_out,
       or_10_out, or_11_out, or_12_out, or_13_out, or_14_out, or_15_out, or_16_out, pull_resistor_12_node,
       pull_resistor_14_node, pull_resistor_16_node, pull_resistor_18_node, SEL0, SEL2, SEL4, SEL6;
  wire [1:0] counter_1_q, n16_bit_line_driver_lvc16244_1_p9, pull_resistor_7_node, pull_resistor_8_node,
       pull_resistor_9_node, pull_resistor_10_node;
  wire [1:1] n16_bit_latch_lvc16373_1_p8, n16_bit_latch_lvc16373_2_p8, n16_bit_latch_lvc16373_3_p8,
       n16_bit_latch_lvc16373_4_p8;
  wire [3:0] n2_to_4_decoder_lvc139_1_p5, n2_to_4_decoder_lvc139_1_p6, n2_to_4_decoder_lvc139_2_p5,
       n2_to_4_decoder_lvc139_2_p6, n16_bit_line_driver_lvc16244_1_p10, n16_bit_line_driver_lvc16244_1_p12_2;
  wire [3:2] n16_bit_line_driver_lvc16244_1_p12;
  wire [3:3] pull_resistor_1_node, pull_resistor_2_node, pull_resistor_3_node, pull_resistor_4_node;
  wire [7:0] controlled_buffer_1_out, controlled_buffer_3_out, controlled_buffer_5_out,
       controlled_buffer_7_out, n8_bit_bi_latch_lvc543_5_p4, n8_bit_bi_latch_lvc543_6_p4,
       n8_bit_bi_latch_lvc543_7_p4, n8_bit_bi_latch_lvc543_8_p4;
  wire [7:4] n16_bit_line_driver_lvc16244_1_p11;
  wire [7:6] n16_bit_latch_lvc16373_1_p7, n16_bit_latch_lvc16373_2_p7, n16_bit_latch_lvc16373_3_p7,
       n16_bit_latch_lvc16373_4_p7;

  Counter #(.width(2), .max('h3)) counter_1 (.Q(counter_1_q), .clk(FST_t));  // open: load, D, count, carry, up, clr
  Clock clock_1 (.out(FST_t));
  not not_1 (SEL4, decoder_1_out0);
  not not_2 (SEL6, decoder_1_out1);
  not not_3 (SEL0, decoder_1_out2);
  not not_4 (SEL2, decoder_1_out3);
  Decoder #(.select(2)) decoder_1 (
    .out0(decoder_1_out0), .out1(decoder_1_out1), .out2(decoder_1_out2), .out3(decoder_1_out3),
    .sel(counter_1_q));  // open: en
  LED led_1 (.in(MPU_0_DEVICE_VALID));
  LED led_2 (.in(MPU_1_DEVICE_VALID));
  LED led_3 (.in(MPU_2_DEVICE_VALID_t));
  LED led_4 (.in(MPU_3_DEVICE_VALID_t));
  assign controlled_buffer_1_out = and_1_out ? MPU_0_D_IN : 8'bz;  // Controlled_Buffer controlled_buffer_1
  assign MPU_0_D_OUT = and_2_out ? controlled_buffer_1_out : 8'bz;  // Controlled_Buffer controlled_buffer_2
  and and_1 (and_1_out, MPU_0_DEVICE_VALID, MPU_0_RWB_B);
  and and_2 (and_2_out, MPU_0_DEVICE_VALID, MPU_0_RWB);
  assign controlled_buffer_3_out = and_3_out ? MPU_1_D_IN : 8'bz;  // Controlled_Buffer controlled_buffer_3
  assign MPU_1_D_OUT = and_4_out ? controlled_buffer_3_out : 8'bz;  // Controlled_Buffer controlled_buffer_4
  and and_3 (and_3_out, MPU_1_DEVICE_VALID, MPU_1_RWB_B);
  and and_4 (and_4_out, MPU_1_DEVICE_VALID, MPU_1_RWB);
  assign controlled_buffer_5_out = and_5_out ? MPU_2_D_IN : 8'bz;  // Controlled_Buffer controlled_buffer_5
  assign MPU_2_D_OUT = and_6_out ? controlled_buffer_5_out : 8'bz;  // Controlled_Buffer controlled_buffer_6
  and and_5 (and_5_out, MPU_2_DEVICE_VALID_t, MPU_2_RWB_B);
  and and_6 (and_6_out, MPU_2_DEVICE_VALID_t, MPU_2_RWB);
  assign controlled_buffer_7_out = and_7_out ? MPU_3_D_IN : 8'bz;  // Controlled_Buffer controlled_buffer_7
  assign MPU_3_D_OUT = and_8_out ? controlled_buffer_7_out : 8'bz;  // Controlled_Buffer controlled_buffer_8
  and and_7 (and_7_out, MPU_3_DEVICE_VALID_t, MPU_3_RWB_B);
  and and_8 (and_8_out, MPU_3_DEVICE_VALID_t, MPU_3_RWB);
  not not_5 (MPU_0_DEVICE_VALID, MPU_0_DEVICE_VALID_B);
  not not_6 (MPU_1_DEVICE_VALID, MPU_1_DEVICE_VALID_B);
  not not_7 (MPU_2_DEVICE_VALID_t, MPU_2_DEVICE_VALID);
  not not_8 (MPU_3_DEVICE_VALID_t, MPU_3_DEVICE_VALID);
  not not_9 (MPU_0_RWB_B, MPU_0_RWB);
  not not_10 (MPU_1_RWB_B, MPU_1_RWB);
  not not_11 (MPU_2_RWB_B, MPU_2_RWB);
  not not_12 (MPU_3_RWB_B, MPU_3_RWB);
  Pull_Resistor pull_resistor_1 (.node(pull_resistor_1_node[3]));
  Pull_Resistor pull_resistor_2 (.node(pull_resistor_2_node[3]));
  Pull_Resistor pull_resistor_3 (.node(pull_resistor_3_node[3]));
  Pull_Resistor pull_resistor_4 (.node(pull_resistor_4_node[3]));
  or or_1 (or_1_out, MPU_0_RWB_B, SEL4);
  // Probe on controlled_buffer_1_out
  or or_2 (or_2_out, MPU_1_RWB_B, SEL6);
  // Probe on controlled_buffer_3_out
  or or_3 (or_3_out, MPU_2_RWB_B, SEL0);
  // Probe on controlled_buffer_5_out
  or or_4 (or_4_out, MPU_3_RWB_B, SEL2);
  // Probe on controlled_buffer_7_out
  // _8_bit_Bi_latch__LVC543 8_bit_bi_latch_lvc543_1: pin names not known; wires that end beside it: MPU_0_RWB, MPU_0_RWB, SEL4, controlled_buffer_1_out, n8_bit_bi_latch_lvc543_1_p5, or_1_out, MPU_0_RWB_B, MPU_0_DEVICE_VALID_B
  // _16_bit_Line_Driver__LVC16244 16_bit_line_driver_lvc16244_1: pin names not known; wires that end beside it: SEL4, SEL4, SEL4, SEL4, {MPU_0_DEVICE_IDENTIFIER[5:4], MPU_0_RWB, MPU_0_RWB_B}, MPU_0_DEVICE_IDENTIFIER[3:0], MPU_0_DEVICE_ADDRESS, {{3{pull_resistor_1_node[3]}}, MPU_0_DEVICE_VALID_B}, {n16_bit_line_driver_lvc16244_1_p9, n16_bit_line_driver_lvc16244_1_p12_2[2], n16_bit_line_driver_lvc16244_1_p12_2[3]}, n16_bit_line_driver_lvc16244_1_p10, n16_bit_line_driver_lvc16244_1_p11, {n16_bit_line_driver_lvc16244_1_p12, n16_bit_line_driver_lvc16244_1_p12_2[1:0]}
  // _8_bit_Bi_latch__LVC543 8_bit_bi_latch_lvc543_2: pin names not known; wires that end beside it: MPU_1_RWB, MPU_1_RWB, SEL6, controlled_buffer_3_out, n8_bit_bi_latch_lvc543_1_p5, or_2_out, MPU_1_RWB_B, MPU_1_DEVICE_VALID_B
  // _16_bit_Line_Driver__LVC16244 16_bit_line_driver_lvc16244_2: pin names not known; wires that end beside it: SEL6, SEL6, SEL6, SEL6, {MPU_1_DEVICE_IDENTIFIER[5:4], MPU_1_RWB, MPU_1_RWB_B}, MPU_1_DEVICE_IDENTIFIER[3:0], MPU_1_DEVICE_ADDRESS, {{3{pull_resistor_2_node[3]}}, MPU_1_DEVICE_VALID_B}, {n16_bit_line_driver_lvc16244_1_p9, n16_bit_line_driver_lvc16244_1_p12_2[2], n16_bit_line_driver_lvc16244_1_p12_2[3]}, n16_bit_line_driver_lvc16244_1_p10, n16_bit_line_driver_lvc16244_1_p11, {n16_bit_line_driver_lvc16244_1_p12, n16_bit_line_driver_lvc16244_1_p12_2[1:0]}
  // _8_bit_Bi_latch__LVC543 8_bit_bi_latch_lvc543_3: pin names not known; wires that end beside it: controlled_buffer_5_out, MPU_2_RWB, MPU_2_RWB, SEL0, controlled_buffer_5_out, n8_bit_bi_latch_lvc543_1_p5, or_3_out, MPU_2_RWB_B, MPU_2_DEVICE_VALID
  // _16_bit_Line_Driver__LVC16244 16_bit_line_driver_lvc16244_3: pin names not known; wires that end beside it: SEL0, SEL0, SEL0, SEL0, {MPU_2_DEVICE_IDENTIFIER[5:4], MPU_2_RWB, MPU_2_RWB_B}, MPU_2_DEVICE_IDENTIFIER[3:0], MPU_2_DEVICE_ADDRESS, {{3{pull_resistor_3_node[3]}}, MPU_2_DEVICE_VALID}, {n16_bit_line_driver_lvc16244_1_p9, n16_bit_line_driver_lvc16244_1_p12_2[2], n16_bit_line_driver_lvc16244_1_p12_2[3]}, n16_bit_line_driver_lvc16244_1_p10, n16_bit_line_driver_lvc16244_1_p11, {n16_bit_line_driver_lvc16244_1_p12, n16_bit_line_driver_lvc16244_1_p12_2[1:0]}
  // _8_bit_Bi_latch__LVC543 8_bit_bi_latch_lvc543_4: pin names not known; wires that end beside it: MPU_3_RWB, MPU_3_RWB, SEL2, controlled_buffer_7_out, n8_bit_bi_latch_lvc543_1_p5, or_4_out, MPU_3_RWB_B, MPU_3_DEVICE_VALID
  // _16_bit_Line_Driver__LVC16244 16_bit_line_driver_lvc16244_4: pin names not known; wires that end beside it: SEL2, SEL2, SEL2, SEL2, {MPU_3_DEVICE_IDENTIFIER[5:4], MPU_3_RWB, MPU_3_RWB_B}, MPU_3_DEVICE_IDENTIFIER[3:0], MPU_3_DEVICE_ADDRESS, {{3{pull_resistor_4_node[3]}}, MPU_3_DEVICE_VALID}, {n16_bit_line_driver_lvc16244_1_p9, n16_bit_line_driver_lvc16244_1_p12_2[2], n16_bit_line_driver_lvc16244_1_p12_2[3]}, n16_bit_line_driver_lvc16244_1_p10, n16_bit_line_driver_lvc16244_1_p11, {n16_bit_line_driver_lvc16244_1_p12, n16_bit_line_driver_lvc16244_1_p12_2[1:0]}
  D_Flip_Flop d_ff_1 (.clk(SEL4), .D(MPU_0_DEVICE_VALID_B), .Q(d_ff_1_q));  // open: Qn, preset, reset
  and and_9 (and_9_out, MPU_0_DEVICE_VALID_B, d_ff_1_q);
  D_Flip_Flop d_ff_2 (.clk(SEL6), .D(MPU_1_DEVICE_VALID_B), .Q(d_ff_2_q));  // open: Qn, preset, reset
  and and_10 (and_10_out, d_ff_2_q, MPU_1_DEVICE_VALID_B);
  and and_11 (and_11_out, MPU_2_DEVICE_VALID, d_ff_3_q);
  D_Flip_Flop d_ff_3 (.clk(SEL0), .D(MPU_2_DEVICE_VALID), .Q(d_ff_3_q));  // open: Qn, preset, reset
  D_Flip_Flop d_ff_4 (.clk(SEL2), .D(MPU_3_DEVICE_VALID), .Q(d_ff_4_q));  // open: Qn, preset, reset
  and and_12 (and_12_out, d_ff_4_q, MPU_3_DEVICE_VALID);
  or or_5 (or_5_out, SEL4, and_9_out);
  or or_6 (or_6_out, and_10_out, SEL6);
  or or_7 (or_7_out, SEL0, and_11_out);
  or or_8 (or_8_out, and_12_out, SEL2);
  Pull_Resistor #(.pull(1)) pull_resistor_5 (.node(n8_bit_bi_latch_lvc543_1_p5));
  Pull_Resistor #(.pull(1)) pull_resistor_6 (.node(n8_bit_bi_latch_lvc543_1_p5));
  // _2_to_4_Decoder__LVC139 2_to_4_decoder_lvc139_1: pin names not known; wires that end beside it: or_5_out, or_6_out, MPU_0_DEVICE_CHANNEL, MPU_1_DEVICE_CHANNEL, n2_to_4_decoder_lvc139_1_p5, n2_to_4_decoder_lvc139_1_p6
  // _2_to_4_Decoder__LVC139 2_to_4_decoder_lvc139_2: pin names not known; wires that end beside it: or_7_out, or_8_out, MPU_2_DEVICE_CHANNEL, MPU_3_DEVICE_CHANNEL, n2_to_4_decoder_lvc139_2_p5, n2_to_4_decoder_lvc139_2_p6
  // _4_bit_Line_Driver__LVC125 4_bit_line_driver_lvc125_1: pin names not known; wires that end beside it: SEL4, SEL4, SEL4, SEL4, n2_to_4_decoder_lvc139_1_p5[0], n2_to_4_decoder_lvc139_1_p5[1], n2_to_4_decoder_lvc139_1_p5[2], n2_to_4_decoder_lvc139_1_p5[3], n4_bit_line_driver_lvc125_1_p9, n4_bit_line_driver_lvc125_1_p10, n4_bit_line_driver_lvc125_1_p11, n4_bit_line_driver_lvc125_1_p12
  // _4_bit_Line_Driver__LVC125 4_bit_line_driver_lvc125_2: pin names not known; wires that end beside it: SEL6, SEL6, SEL6, SEL6, n2_to_4_decoder_lvc139_1_p6[0], n2_to_4_decoder_lvc139_1_p6[1], n2_to_4_decoder_lvc139_1_p6[2], n2_to_4_decoder_lvc139_1_p6[3], n4_bit_line_driver_lvc125_1_p9, n4_bit_line_driver_lvc125_1_p10, n4_bit_line_driver_lvc125_1_p11, n4_bit_line_driver_lvc125_1_p12
  // _4_bit_Line_Driver__LVC125 4_bit_line_driver_lvc125_3: pin names not known; wires that end beside it: SEL0, SEL0, SEL0, SEL0, n2_to_4_decoder_lvc139_2_p5[0], n2_to_4_decoder_lvc139_2_p5[1], n2_to_4_decoder_lvc139_2_p5[2], n2_to_4_decoder_lvc139_2_p5[3], n4_bit_line_driver_lvc125_1_p9, n4_bit_line_driver_lvc125_1_p10, n4_bit_line_driver_lvc125_1_p11, n4_bit_line_driver_lvc125_1_p12
  // _4_bit_Line_Driver__LVC125 4_bit_line_driver_lvc125_4: pin names not known; wires that end beside it: SEL2, SEL2, SEL2, SEL2, n2_to_4_decoder_lvc139_2_p6[0], n2_to_4_decoder_lvc139_2_p6[1], n2_to_4_decoder_lvc139_2_p6[2], n2_to_4_decoder_lvc139_2_p6[3], n4_bit_line_driver_lvc125_1_p9, n4_bit_line_driver_lvc125_1_p10, n4_bit_line_driver_lvc125_1_p11, n4_bit_line_driver_lvc125_1_p12
  or or_9 (or_9_out, n4_bit_line_driver_lvc125_1_p9, n16_bit_line_driver_lvc16244_1_p12_2[3]);
  or or_10 (or_10_out, n4_bit_line_driver_lvc125_1_p9, FST_t, n16_bit_line_driver_lvc16244_1_p12_2[2]);
  // Probe on n8_bit_bi_latch_lvc543_1_p5
  Pull_Resistor pull_resistor_7 (.node(pull_resistor_7_node));
  nor nor_1 (nor_1_out, n4_bit_line_driver_lvc125_1_p9, FST_t);
  or or_11 (or_11_out, n4_bit_line_driver_lvc125_1_p10, n16_bit_line_driver_lvc16244_1_p12_2[3]);
  or or_12 (or_12_out, n4_bit_line_driver_lvc125_1_p10, FST_t, n16_bit_line_driver_lvc16244_1_p12_2[2]);
  // Probe on n8_bit_bi_latch_lvc543_1_p5
  Pull_Resistor pull_resistor_8 (.node(pull_resistor_8_node));
  nor nor_2 (nor_2_out, n4_bit_line_driver_lvc125_1_p10, FST_t);
  or or_13 (or_13_out, n4_bit_line_driver_lvc125_1_p11, n16_bit_line_driver_lvc16244_1_p12_2[3]);
  or or_14 (or_14_out, n4_bit_line_driver_lvc125_1_p11, FST_t, n16_bit_line_driver_lvc16244_1_p12_2[2]);
  // Probe on n8_bit_bi_latch_lvc543_1_p5
  Pull_Resistor pull_resistor_9 (.node(pull_resistor_9_node));
  nor nor_3 (nor_3_out, n4_bit_line_driver_lvc125_1_p11, FST_t);
  or or_15 (or_15_out, n4_bit_line_driver_lvc125_1_p12, n16_bit_line_driver_lvc16244_1_p12_2[3]);
  or or_16 (or_16_out, n4_bit_line_driver_lvc125_1_p12, FST_t, n16_bit_line_driver_lvc16244_1_p12_2[2]);
  // Probe on n8_bit_bi_latch_lvc543_1_p5
  Pull_Resistor pull_resistor_10 (.node(pull_resistor_10_node));
  nor nor_4 (nor_4_out, n4_bit_line_driver_lvc125_1_p12, FST_t);
  Pull_Resistor pull_resistor_11 ();  // open: node
  Pull_Resistor pull_resistor_12 (.node(pull_resistor_12_node));
  Pull_Resistor pull_resistor_13 ();  // open: node
  Pull_Resistor pull_resistor_14 (.node(pull_resistor_14_node));
  Pull_Resistor pull_resistor_15 ();  // open: node
  Pull_Resistor pull_resistor_16 (.node(pull_resistor_16_node));
  Pull_Resistor pull_resistor_17 ();  // open: node
  Pull_Resistor pull_resistor_18 (.node(pull_resistor_18_node));
  // _8_bit_Bi_latch__LVC543 8_bit_bi_latch_lvc543_5: pin names not known; wires that end beside it: or_10_out, CH_0_RWB, n8_bit_bi_latch_lvc543_1_p5, n8_bit_bi_latch_lvc543_5_p4, CH_0_RWB_B, or_9_out, CH_0_DEVICE_VALID_B
  // _16_bit_Latch__LVC16373 16_bit_latch_lvc16373_1: pin names not known; wires that end beside it: pull_resistor_12_node, pull_resistor_12_node, {pull_resistor_7_node, n16_bit_line_driver_lvc16244_1_p9, n16_bit_line_driver_lvc16244_1_p10}, nor_1_out, {n16_bit_line_driver_lvc16244_1_p11, n16_bit_line_driver_lvc16244_1_p12_2}, nor_1_out, {n16_bit_latch_lvc16373_1_p7, CH_0_DEVICE_IDENTIFIER}, {CH_0_DEVICE_ADDRESS, CH_0_RWB_B, CH_0_RWB, n16_bit_latch_lvc16373_1_p8[1], CH_0_DEVICE_VALID_B}
  // _8_bit_Bi_latch__LVC543 8_bit_bi_latch_lvc543_6: pin names not known; wires that end beside it: or_12_out, CH_1_RWB, n8_bit_bi_latch_lvc543_1_p5, n8_bit_bi_latch_lvc543_6_p4, CH_1_RWB_B, or_11_out, CH_1_DEVICE_VALID_B
  // _16_bit_Latch__LVC16373 16_bit_latch_lvc16373_2: pin names not known; wires that end beside it: pull_resistor_14_node, pull_resistor_14_node, {pull_resistor_8_node, n16_bit_line_driver_lvc16244_1_p9, n16_bit_line_driver_lvc16244_1_p10}, nor_2_out, {n16_bit_line_driver_lvc16244_1_p11, n16_bit_line_driver_lvc16244_1_p12_2}, nor_2_out, {n16_bit_latch_lvc16373_2_p7, CH_1_DEVICE_IDENTIFIER}, {CH_1_DEVICE_ADDRESS, CH_1_RWB_B, CH_1_RWB, n16_bit_latch_lvc16373_2_p8[1], CH_1_DEVICE_VALID_B}
  // _8_bit_Bi_latch__LVC543 8_bit_bi_latch_lvc543_7: pin names not known; wires that end beside it: or_14_out, CH_2_RWB, n8_bit_bi_latch_lvc543_1_p5, n8_bit_bi_latch_lvc543_7_p4, CH_2_RWB_B, or_13_out, CH_2_DEVICE_VALID_B
  // _16_bit_Latch__LVC16373 16_bit_latch_lvc16373_3: pin names not known; wires that end beside it: pull_resistor_16_node, pull_resistor_16_node, {pull_resistor_9_node, n16_bit_line_driver_lvc16244_1_p9, n16_bit_line_driver_lvc16244_1_p10}, nor_3_out, {n16_bit_line_driver_lvc16244_1_p11, n16_bit_line_driver_lvc16244_1_p12_2}, nor_3_out, {n16_bit_latch_lvc16373_3_p7, CH_2_DEVICE_IDENTIFIER}, {CH_2_DEVICE_ADDRESS, CH_2_RWB_B, CH_2_RWB, n16_bit_latch_lvc16373_3_p8[1], CH_2_DEVICE_VALID_B}
  // _8_bit_Bi_latch__LVC543 8_bit_bi_latch_lvc543_8: pin names not known; wires that end beside it: or_16_out, CH_3_RWB, n8_bit_bi_latch_lvc543_1_p5, n8_bit_bi_latch_lvc543_8_p4, CH_3_RWB_B, or_15_out, CH_3_DEVICE_VALID_B
  // _16_bit_Latch__LVC16373 16_bit_latch_lvc16373_4: pin names not known; wires that end beside it: pull_resistor_18_node, pull_resistor_18_node, {pull_resistor_10_node, n16_bit_line_driver_lvc16244_1_p9, n16_bit_line_driver_lvc16244_1_p10}, nor_4_out, {n16_bit_line_driver_lvc16244_1_p11, n16_bit_line_driver_lvc16244_1_p12_2}, nor_4_out, {n16_bit_latch_lvc16373_4_p7, CH_3_DEVICE_IDENTIFIER}, {CH_3_DEVICE_ADDRESS, CH_3_RWB_B, CH_3_RWB, n16_bit_latch_lvc16373_4_p8[1], CH_3_DEVICE_VALID_B}
  assign n8_bit_bi_latch_lvc543_5_p4 = CH_0_RWB ? CH_0_D_IN : 8'bz;  // Controlled_Buffer controlled_buffer_9
  Pull_Resistor #(.pull(1)) pull_resistor_19 (.node(CH_0_D_IN));
  assign CH_0_D_OUT = CH_0_RWB_B ? n8_bit_bi_latch_lvc543_5_p4 : 8'bz;  // Controlled_Buffer controlled_buffer_10
  Pull_Resistor #(.pull(1)) pull_resistor_20 (.node(CH_0_D_OUT));
  LED led_5 (.in(CH_0_DEVICE_VALID_B));
  Pull_Resistor #(.pull(1)) pull_resistor_21 (.node(CH_1_D_IN));
  assign n8_bit_bi_latch_lvc543_6_p4 = CH_1_RWB ? CH_1_D_IN : 8'bz;  // Controlled_Buffer controlled_buffer_11
  Pull_Resistor #(.pull(1)) pull_resistor_22 (.node(CH_1_D_OUT));
  assign CH_1_D_OUT = CH_1_RWB_B ? n8_bit_bi_latch_lvc543_6_p4 : 8'bz;  // Controlled_Buffer controlled_buffer_12
  LED led_6 (.in(CH_1_DEVICE_VALID_B));
  Pull_Resistor #(.pull(1)) pull_resistor_23 (.node(CH_2_D_IN));
  assign n8_bit_bi_latch_lvc543_7_p4 = CH_2_RWB ? CH_2_D_IN : 8'bz;  // Controlled_Buffer controlled_buffer_13
  Pull_Resistor #(.pull(1)) pull_resistor_24 (.node(CH_2_D_OUT));
  assign CH_2_D_OUT = CH_2_RWB_B ? n8_bit_bi_latch_lvc543_7_p4 : 8'bz;  // Controlled_Buffer controlled_buffer_14
  LED led_7 (.in(CH_2_DEVICE_VALID_B));
  assign n8_bit_bi_latch_lvc543_8_p4 = CH_3_RWB ? CH_3_D_IN : 8'bz;  // Controlled_Buffer controlled_buffer_15
  Pull_Resistor #(.pull(1)) pull_resistor_25 (.node(CH_3_D_IN));
  Pull_Resistor #(.pull(1)) pull_resistor_26 (.node(CH_3_D_OUT));
  assign CH_3_D_OUT = CH_3_RWB_B ? n8_bit_bi_latch_lvc543_8_p4 : 8'bz;  // Controlled_Buffer controlled_buffer_16
  LED led_8 (.in(CH_3_DEVICE_VALID_B));
endmodule
